// Digital circuit paddle_controla.dig as structural Verilog
module paddle_controla (
  input  in_1,
  input  in_2,
  input  clk,
  output out_4,
  output out_5
);

  wire xor_1_out;

  xor xor_1 (xor_1_out, in_1, in_2);
  and and_1 (out_4, clk, xor_1_out);
  // _74193 _74193_1: pin names not known

  assign out_5 = clk;
endmodule
