// Digital circuit paddle_controla_74193.dig as structural Verilog
module paddle_controla_74193 (
  input  in_5,
  input  in_6,
  input  in_7,
  input  in_8,
  input  in_9,
  input  in_10,
  input  in_11,
  input  in_14,
  output out_1,
  output out_2,
  output out_3,
  output out_4,
  output out_12,
  output out_13
);

  _74193 _74193_1 (
    .pin1(in_7), .pin2(out_3), .pin3(out_4), .pin4(in_5), .pin5(in_6), .pin6(out_2), .pin7(out_1),
    .pin8(1'b0), .pin9(in_10), .pin10(in_9), .pin11(in_11), .pin12(out_12), .pin13(out_13), .pin14(in_14),
    .pin15(in_8), .pin16(1'b1));
endmodule
