// Digital circuit c1.dig as structural Verilog
module c1 (
  input  paddle_down,
  input  paddle_up,
  input  paddle_load_n,
  input  paddle_clear,
  input  paddle_q2_in,
  input  paddle_q3_in,
  input  paddle_q1_in,
  input  paddle_q0_in,
  input  pixel_clock,
  input  xscan_low_clear_n,
  input  xscan_low_enp,
  input  xscan_low_load_n,
  input  xscan_low_ent,
  input  xscan_mid_clear_n,
  input  xscan_mid_enp,
  input  xscan_mid_load_n,
  input  xscan_high_clear_n,
  input  xscan_high_enp,
  input  xscan_high_load_n,
  output paddle_d0,
  output paddle_d1,
  output paddle_d2,
  output paddle_d3,
  output paddle_borrow_out,
  output paddle_carry_out,
  output b0,
  output b1,
  output b2,
  output b3,
  output b4,
  output b5,
  output b6,
  output b7,
  output b8,
  output b9,
  output b10,
  output b11,
  output xscan_high_rco
);

  wire _7485_1_p3, _7485_1_p4, _7485_1_p5, _7485_2_pin6, _7485_2_pin7, x_scan_bits_0_3_pin15,
       x_scan_bits_4_7_pin15;

  _74193 x_paddle_counter (
    .pin1(paddle_load_n), .pin2(paddle_d2), .pin3(paddle_d3), .pin4(paddle_down), .pin5(paddle_up),
    .pin6(paddle_d1), .pin7(paddle_d0), .pin8(1'b0), .pin9(paddle_q3_in), .pin10(paddle_q2_in),
    .pin11(paddle_q1_in), .pin12(paddle_borrow_out), .pin13(paddle_carry_out), .pin14(paddle_q0_in),
    .pin15(paddle_clear), .pin16(1'b1));
  // _7485 _7485_1: pin names not known; wires that end beside it: 1'b1, 1'b0, _7485_1_p3, _7485_1_p4, _7485_1_p5, 1'b0
  _74163 x_scan_bits_0_3 (
    .pin1(xscan_low_clear_n), .pin2(pixel_clock), .pin3(1'b0), .pin4(1'b0), .pin5(1'b0), .pin6(1'b0),
    .pin7(xscan_low_enp), .pin8(1'b0), .pin9(xscan_low_load_n), .pin10(xscan_low_ent), .pin11(b3),
    .pin12(b2), .pin13(b1), .pin14(b0), .pin15(x_scan_bits_0_3_pin15), .pin16(1'b1));
  _7485 _7485_2 (
    .pin2(_7485_1_p3), .pin3(_7485_1_p4), .pin4(_7485_1_p5), .pin5(1'b0), .pin6(_7485_2_pin6),
    .pin7(_7485_2_pin7), .pin8(1'b0), .pin16(1'b1));  // open: pin1, pin9, pin10, pin11, pin12, pin13, pin14, pin15
  // _7485 _7485_3: pin names not known; wires that end beside it: 1'b0, _7485_2_pin6, _7485_2_pin7, 1'b0, 1'b1
  _74163 x_scan_bits_4_7 (
    .pin1(xscan_mid_clear_n), .pin2(pixel_clock), .pin3(1'b0), .pin4(1'b0), .pin5(1'b0), .pin6(1'b0),
    .pin7(xscan_mid_enp), .pin8(1'b0), .pin9(xscan_mid_load_n), .pin10(x_scan_bits_0_3_pin15), .pin11(b7),
    .pin12(b6), .pin13(b5), .pin14(b4), .pin15(x_scan_bits_4_7_pin15), .pin16(1'b1));
  _74163 x_scan_bits_8_11 (
    .pin1(xscan_high_clear_n), .pin2(pixel_clock), .pin3(1'b0), .pin4(1'b0), .pin5(1'b0), .pin6(1'b0),
    .pin7(xscan_high_enp), .pin8(1'b0), .pin9(xscan_high_load_n), .pin10(x_scan_bits_4_7_pin15), .pin11(b11),
    .pin12(b10), .pin13(b9), .pin14(b8), .pin15(xscan_high_rco), .pin16(1'b1));

  // Notes on the sheet:
  //   X_Paddle
  //   X_scan
endmodule
