// Digital circuit c1_xscan_compare_656_753.dig as structural Verilog
module c1_xscan_compare_656_753 (
  input  paddle_down,
  input  paddle_up,
  input  paddle_load_n,
  input  paddle_clear,
  input  paddle_q2_in,
  input  paddle_q3_in,
  input  paddle_q1_in,
  input  paddle_q0_in,
  input  pixel_clock,
  input  x_scan_clear_n,
  output paddle_d0,
  output paddle_d1,
  output paddle_d2,
  output paddle_d3,
  output paddle_borrow_out,
  output paddle_carry_out,
  output x_scan_b0,
  output x_scan_b1,
  output x_scan_b2,
  output x_scan_b3,
  output x_scan_b4,
  output x_scan_b5,
  output x_scan_b6,
  output x_scan_b7,
  output x_scan_b8,
  output x_scan_b9,
  output x_scan_gt_656,
  output x_scan_eq_656,
  output x_scan_lt_656,
  output x_scan_gt_753,
  output x_scan_eq_753,
  output x_scan_lt_753,
  output out_33
);

  wire x_scan_cmp656_bits_0_3_pin4, x_scan_cmp656_bits_4_7_p6, x_scan_cmp656_bits_8_11_pin13,
       x_scan_cmp656_bits_8_11_pin15, x_scan_cmp753_bits_0_3_pin4, x_scan_cmp753_bits_4_7_p8,
       x_scan_cmp753_bits_8_11_pin13, x_scan_cmp753_bits_8_11_pin15;

  _74193 x_paddle_counter (
    .pin1(paddle_load_n), .pin2(paddle_d2), .pin3(paddle_d3), .pin4(paddle_down), .pin5(paddle_up),
    .pin6(paddle_d1), .pin7(paddle_d0), .pin8(1'b0), .pin9(paddle_q3_in), .pin10(paddle_q2_in),
    .pin11(paddle_q1_in), .pin12(paddle_borrow_out), .pin13(paddle_carry_out), .pin14(paddle_q0_in),
    .pin15(paddle_clear), .pin16(1'b1));
  _74163 x_scan_counter_bits_0_3 (
    .pin3(1'b0), .pin4(1'b0), .pin5(1'b0), .pin6(1'b0), .pin7(pixel_clock), .pin8(1'b0), .pin9(pixel_clock),
    .pin10(pixel_clock), .pin11(1'b0), .pin12(1'b0), .pin13(1'b0), .pin14(1'b0));  // open: pin1, pin2, pin15, pin16
  _7485 x_scan_cmp656_bits_0_3 (
    .pin2(1'b1), .pin3(1'b0), .pin4(x_scan_cmp656_bits_0_3_pin4), .pin5(1'b0), .pin7(1'b0), .pin8(1'b0),
    .pin10(1'b0), .pin12(1'b0), .pin13(1'b0), .pin15(1'b0));  // open: pin1, pin6, pin9, pin11, pin14, pin16
  _7485 x_scan_cmp753_bits_0_3 (
    .pin2(1'b1), .pin3(1'b0), .pin4(x_scan_cmp753_bits_0_3_pin4), .pin5(1'b0), .pin7(1'b0), .pin8(1'b0),
    .pin10(1'b0), .pin12(1'b0), .pin13(1'b0), .pin15(1'b0));  // open: pin1, pin6, pin9, pin11, pin14, pin16
  _74163 x_scan_counter_bits_4_7 (
    .pin3(1'b0), .pin4(1'b0), .pin5(1'b0), .pin6(1'b0), .pin8(1'b0), .pin9(pixel_clock), .pin10(pixel_clock),
    .pin11(1'b0), .pin12(1'b0), .pin13(1'b0), .pin14(1'b0));  // open: pin1, pin2, pin7, pin15, pin16
  // _7485 x_scan_cmp656_bits_4_7: pin names not known; wires that end beside it: 1'b1, 1'b0, 1'b0, 1'b0, 1'b0, x_scan_cmp656_bits_4_7_p6, 1'b0, 1'b0, 1'b0, x_scan_cmp656_bits_4_7_p6, 1'b1
  // _7485 x_scan_cmp753_bits_4_7: pin names not known; wires that end beside it: 1'b0, 1'b0, 1'b1, 1'b0, 1'b0, 1'b0, 1'b0, x_scan_cmp753_bits_4_7_p8, 1'b0, 1'b0, 1'b0, x_scan_cmp753_bits_4_7_p8, 1'b1
  _74163 x_scan_counter_bits_8_11 (
    .pin1(pixel_clock), .pin2(pixel_clock), .pin3(1'b0), .pin4(1'b0), .pin5(1'b0), .pin6(1'b0), .pin8(1'b0),
    .pin9(pixel_clock), .pin10(pixel_clock), .pin13(x_scan_b8), .pin14(x_scan_b8), .pin16(pixel_clock));  // open: pin7, pin11, pin12, pin15
  _7485 x_scan_cmp656_bits_8_11 (
    .pin1(1'b0), .pin2(1'b0), .pin3(1'b0), .pin4(1'b0), .pin5(x_scan_gt_656), .pin6(1'b0),
    .pin7(x_scan_lt_656), .pin8(1'b0), .pin9(1'b0), .pin10(x_scan_b8), .pin11(1'b0), .pin12(x_scan_b8),
    .pin13(x_scan_cmp656_bits_8_11_pin13), .pin14(1'b0), .pin15(x_scan_cmp656_bits_8_11_pin15), .pin16(1'b1));
  _7485 x_scan_cmp753_bits_8_11 (
    .pin1(1'b0), .pin2(1'b0), .pin3(1'b0), .pin4(1'b0), .pin5(x_scan_gt_753), .pin6(1'b0),
    .pin7(x_scan_lt_753), .pin8(1'b0), .pin9(1'b0), .pin10(x_scan_b8), .pin11(1'b0), .pin12(x_scan_b8),
    .pin13(x_scan_cmp753_bits_8_11_pin13), .pin14(1'b0), .pin15(x_scan_cmp753_bits_8_11_pin15), .pin16(1'b1));
  nand nand_1 (out_33, x_scan_gt_656, x_scan_lt_753);

  assign x_scan_b0 = 1'b0;
  assign x_scan_b1 = 1'b0;
  assign x_scan_b2 = 1'b0;
  assign x_scan_b3 = 1'b0;
  assign x_scan_b4 = 1'b0;
  assign x_scan_b5 = 1'b0;
  assign x_scan_b6 = 1'b0;
  assign x_scan_b7 = 1'b0;
  assign x_scan_b9 = x_scan_b8;
  assign x_scan_clear_n = pixel_clock;
  assign x_scan_eq_656 = 1'b0;
  assign x_scan_eq_753 = 1'b0;
  // also tied to VCC on the sheet: pixel_clock

  // Notes on the sheet:
  //   X_Paddle
  //   HSYNC_START = 656
  //   10 bit: 1010010000
  //   HSYNC_END = 753
  //   10 bit: 1011110001
  //   X_SCAN COUNTER (10 bit usati)
  //   X_SCAN vs HSYNC_START
  //   X_SCAN vs HSYNC_END
endmodule
