// Digital circuit c1_xscan_compare_656_753_800_clear_rebuilt.dig as structural Verilog
module c1_xscan_compare_656_753_800_clear_rebuilt (
  input  paddle_down,
  input  paddle_up,
  input  paddle_load_n,
  input  paddle_clear,
  input  paddle_q2_in,
  input  paddle_q3_in,
  input  paddle_q1_in,
  input  paddle_q0_in,
  input  pixel_clock,
  output paddle_d0,
  output paddle_d1,
  output paddle_d2,
  output paddle_d3,
  output paddle_borrow_out,
  output paddle_carry_out,
  output x_scan_b0,
  output x_scan_b1,
  output x_scan_b2,
  output x_scan_b3,
  output x_scan_b4,
  output x_scan_b5,
  output x_scan_b6,
  output x_scan_b7,
  output x_scan_b8,
  output x_scan_b9,
  output x_scan_gt_656,
  output x_scan_eq_656,
  output x_scan_lt_656,
  output x_scan_gt_753,
  output x_scan_eq_753,
  output x_scan_lt_753,
  output hsync_n,
  output x_scan_gt_800,
  output x_scan_eq_800,
  output x_scan_lt_800,
  output x_scan_clear_n
);

  wire x_scan_clear_inv1_out, x_scan_cmp656_bits_0_3_pin5, x_scan_cmp656_bits_0_3_pin6,
       x_scan_cmp656_bits_0_3_pin7, x_scan_cmp656_bits_4_7_pin5, x_scan_cmp656_bits_4_7_pin6,
       x_scan_cmp656_bits_4_7_pin7, x_scan_cmp753_bits_0_3_pin5, x_scan_cmp753_bits_0_3_pin6,
       x_scan_cmp753_bits_0_3_pin7, x_scan_cmp753_bits_4_7_pin5, x_scan_cmp753_bits_4_7_pin6,
       x_scan_cmp753_bits_4_7_pin7, x_scan_cmp800_bits_0_3_pin5, x_scan_cmp800_bits_0_3_pin6,
       x_scan_cmp800_bits_0_3_pin7, x_scan_cmp800_bits_4_7_pin5, x_scan_cmp800_bits_4_7_pin6,
       x_scan_cmp800_bits_4_7_pin7, x_scan_counter_bits_0_3_pin15, x_scan_counter_bits_4_7_pin15,
       x_scan_counter_bits_8_11_pin11, x_scan_counter_bits_8_11_pin12;
  wire [2:0] x_scan_cmp656_bits_0_3_pin2, x_scan_cmp753_bits_0_3_pin2, x_scan_cmp800_bits_0_3_pin2;
  wire [11:0] x_scan_cmp656_bits_0_3_pin9, x_scan_cmp753_bits_0_3_pin9, x_scan_cmp800_bits_0_3_pin9;

  _74193 x_paddle_counter (
    .pin1(paddle_load_n), .pin2(paddle_d2), .pin3(paddle_d3), .pin4(paddle_down), .pin5(paddle_up),
    .pin6(paddle_d1), .pin7(paddle_d0), .pin8(1'b0), .pin9(paddle_q3_in), .pin10(paddle_q2_in),
    .pin11(paddle_q1_in), .pin12(paddle_borrow_out), .pin13(paddle_carry_out), .pin14(paddle_q0_in),
    .pin15(paddle_clear), .pin16(1'b1));
  _74163 x_scan_counter_bits_0_3 (
    .pin1(x_scan_clear_n), .pin2(pixel_clock), .pin3(1'b0), .pin4(1'b0), .pin5(1'b0), .pin6(1'b0),
    .pin7(1'b1), .pin8(1'b0), .pin9(1'b1), .pin10(1'b1), .pin11(x_scan_b3), .pin12(x_scan_b2),
    .pin13(x_scan_b1), .pin14(x_scan_b0), .pin15(x_scan_counter_bits_0_3_pin15), .pin16(1'b1));
  _7485 x_scan_cmp656_bits_0_3 (
    .pin1(x_scan_cmp656_bits_0_3_pin9[3]), .pin2(x_scan_cmp656_bits_0_3_pin2[0]),
    .pin3(x_scan_cmp656_bits_0_3_pin2[1]), .pin4(x_scan_cmp656_bits_0_3_pin2[2]),
    .pin5(x_scan_cmp656_bits_0_3_pin5), .pin6(x_scan_cmp656_bits_0_3_pin6),
    .pin7(x_scan_cmp656_bits_0_3_pin7), .pin8(1'b0), .pin9(x_scan_cmp656_bits_0_3_pin9[0]),
    .pin10(x_scan_b0), .pin11(x_scan_cmp656_bits_0_3_pin9[1]), .pin12(x_scan_b1), .pin13(x_scan_b2),
    .pin14(x_scan_cmp656_bits_0_3_pin9[2]), .pin15(x_scan_b3), .pin16(1'b1));
  _7485 x_scan_cmp753_bits_0_3 (
    .pin1(x_scan_cmp753_bits_0_3_pin9[3]), .pin2(x_scan_cmp753_bits_0_3_pin2[0]),
    .pin3(x_scan_cmp753_bits_0_3_pin2[1]), .pin4(x_scan_cmp753_bits_0_3_pin2[2]),
    .pin5(x_scan_cmp753_bits_0_3_pin5), .pin6(x_scan_cmp753_bits_0_3_pin6),
    .pin7(x_scan_cmp753_bits_0_3_pin7), .pin8(1'b0), .pin9(x_scan_cmp753_bits_0_3_pin9[0]),
    .pin10(x_scan_b0), .pin11(x_scan_cmp753_bits_0_3_pin9[1]), .pin12(x_scan_b1), .pin13(x_scan_b2),
    .pin14(x_scan_cmp753_bits_0_3_pin9[2]), .pin15(x_scan_b3), .pin16(1'b1));
  _7485 x_scan_cmp800_bits_0_3 (
    .pin1(x_scan_cmp800_bits_0_3_pin9[3]), .pin2(x_scan_cmp800_bits_0_3_pin2[0]),
    .pin3(x_scan_cmp800_bits_0_3_pin2[1]), .pin4(x_scan_cmp800_bits_0_3_pin2[2]),
    .pin5(x_scan_cmp800_bits_0_3_pin5), .pin6(x_scan_cmp800_bits_0_3_pin6),
    .pin7(x_scan_cmp800_bits_0_3_pin7), .pin8(1'b0), .pin9(x_scan_cmp800_bits_0_3_pin9[0]),
    .pin10(x_scan_b0), .pin11(x_scan_cmp800_bits_0_3_pin9[1]), .pin12(x_scan_b1), .pin13(x_scan_b2),
    .pin14(x_scan_cmp800_bits_0_3_pin9[2]), .pin15(x_scan_b3), .pin16(1'b1));
  _74163 x_scan_counter_bits_4_7 (
    .pin1(x_scan_clear_n), .pin2(pixel_clock), .pin3(1'b0), .pin4(1'b0), .pin5(1'b0), .pin6(1'b0),
    .pin7(1'b1), .pin8(1'b0), .pin9(1'b1), .pin10(x_scan_counter_bits_0_3_pin15), .pin11(x_scan_b7),
    .pin12(x_scan_b6), .pin13(x_scan_b5), .pin14(x_scan_b4), .pin15(x_scan_counter_bits_4_7_pin15),
    .pin16(1'b1));
  _7485 x_scan_cmp656_bits_4_7 (
    .pin1(x_scan_cmp656_bits_0_3_pin9[7]), .pin2(x_scan_cmp656_bits_0_3_pin7),
    .pin3(x_scan_cmp656_bits_0_3_pin6), .pin4(x_scan_cmp656_bits_0_3_pin5),
    .pin5(x_scan_cmp656_bits_4_7_pin5), .pin6(x_scan_cmp656_bits_4_7_pin6),
    .pin7(x_scan_cmp656_bits_4_7_pin7), .pin8(1'b0), .pin9(x_scan_cmp656_bits_0_3_pin9[4]),
    .pin10(x_scan_b4), .pin11(x_scan_cmp656_bits_0_3_pin9[5]), .pin12(x_scan_b5), .pin13(x_scan_b6),
    .pin14(x_scan_cmp656_bits_0_3_pin9[6]), .pin15(x_scan_b7), .pin16(1'b1));
  _7485 x_scan_cmp753_bits_4_7 (
    .pin1(x_scan_cmp753_bits_0_3_pin9[7]), .pin2(x_scan_cmp753_bits_0_3_pin7),
    .pin3(x_scan_cmp753_bits_0_3_pin6), .pin4(x_scan_cmp753_bits_0_3_pin5),
    .pin5(x_scan_cmp753_bits_4_7_pin5), .pin6(x_scan_cmp753_bits_4_7_pin6),
    .pin7(x_scan_cmp753_bits_4_7_pin7), .pin8(1'b0), .pin9(x_scan_cmp753_bits_0_3_pin9[4]),
    .pin10(x_scan_b4), .pin11(x_scan_cmp753_bits_0_3_pin9[5]), .pin12(x_scan_b5), .pin13(x_scan_b6),
    .pin14(x_scan_cmp753_bits_0_3_pin9[6]), .pin15(x_scan_b7), .pin16(1'b1));
  _7485 x_scan_cmp800_bits_4_7 (
    .pin1(x_scan_cmp800_bits_0_3_pin9[7]), .pin2(x_scan_cmp800_bits_0_3_pin7),
    .pin3(x_scan_cmp800_bits_0_3_pin6), .pin4(x_scan_cmp800_bits_0_3_pin5),
    .pin5(x_scan_cmp800_bits_4_7_pin5), .pin6(x_scan_cmp800_bits_4_7_pin6),
    .pin7(x_scan_cmp800_bits_4_7_pin7), .pin8(1'b0), .pin9(x_scan_cmp800_bits_0_3_pin9[4]),
    .pin10(x_scan_b4), .pin11(x_scan_cmp800_bits_0_3_pin9[5]), .pin12(x_scan_b5), .pin13(x_scan_b6),
    .pin14(x_scan_cmp800_bits_0_3_pin9[6]), .pin15(x_scan_b7), .pin16(1'b1));
  _74163 x_scan_counter_bits_8_11 (
    .pin1(x_scan_clear_n), .pin2(pixel_clock), .pin3(1'b0), .pin4(1'b0), .pin5(1'b0), .pin6(1'b0),
    .pin7(1'b1), .pin8(1'b0), .pin9(1'b1), .pin10(x_scan_counter_bits_4_7_pin15),
    .pin11(x_scan_counter_bits_8_11_pin11), .pin12(x_scan_counter_bits_8_11_pin12), .pin13(x_scan_b9),
    .pin14(x_scan_b8), .pin16(1'b1));  // open: pin15
  _7485 x_scan_cmp656_bits_8_11 (
    .pin1(x_scan_cmp656_bits_0_3_pin9[11]), .pin2(x_scan_cmp656_bits_4_7_pin7),
    .pin3(x_scan_cmp656_bits_4_7_pin6), .pin4(x_scan_cmp656_bits_4_7_pin5), .pin5(x_scan_gt_656),
    .pin6(x_scan_eq_656), .pin7(x_scan_lt_656), .pin8(1'b0), .pin9(x_scan_cmp656_bits_0_3_pin9[8]),
    .pin10(x_scan_b8), .pin11(x_scan_cmp656_bits_0_3_pin9[9]), .pin12(x_scan_b9),
    .pin13(x_scan_counter_bits_8_11_pin12), .pin14(x_scan_cmp656_bits_0_3_pin9[10]),
    .pin15(x_scan_counter_bits_8_11_pin11), .pin16(1'b1));
  _7485 x_scan_cmp753_bits_8_11 (
    .pin1(x_scan_cmp753_bits_0_3_pin9[11]), .pin2(x_scan_cmp753_bits_4_7_pin7),
    .pin3(x_scan_cmp753_bits_4_7_pin6), .pin4(x_scan_cmp753_bits_4_7_pin5), .pin5(x_scan_gt_753),
    .pin6(x_scan_eq_753), .pin7(x_scan_lt_753), .pin8(1'b0), .pin9(x_scan_cmp753_bits_0_3_pin9[8]),
    .pin10(x_scan_b8), .pin11(x_scan_cmp753_bits_0_3_pin9[9]), .pin12(x_scan_b9),
    .pin13(x_scan_counter_bits_8_11_pin12), .pin14(x_scan_cmp753_bits_0_3_pin9[10]),
    .pin15(x_scan_counter_bits_8_11_pin11), .pin16(1'b1));
  _7485 x_scan_cmp800_bits_8_11 (
    .pin1(x_scan_cmp800_bits_0_3_pin9[11]), .pin2(x_scan_cmp800_bits_4_7_pin7),
    .pin3(x_scan_cmp800_bits_4_7_pin6), .pin4(x_scan_cmp800_bits_4_7_pin5), .pin5(x_scan_gt_800),
    .pin6(x_scan_eq_800), .pin7(x_scan_lt_800), .pin8(1'b0), .pin9(x_scan_cmp800_bits_0_3_pin9[8]),
    .pin10(x_scan_b8), .pin11(x_scan_cmp800_bits_0_3_pin9[9]), .pin12(x_scan_b9),
    .pin13(x_scan_counter_bits_8_11_pin12), .pin14(x_scan_cmp800_bits_0_3_pin9[10]),
    .pin15(x_scan_counter_bits_8_11_pin11), .pin16(1'b1));
  nand hsync_window_nand (hsync_n, x_scan_gt_656, x_scan_lt_753);
  nand x_scan_clear_inv1 (x_scan_clear_inv1_out, x_scan_lt_800, x_scan_lt_800);
  nand x_scan_clear_inv2 (x_scan_clear_n, x_scan_clear_inv1_out, x_scan_clear_inv1_out);
  // also tied to GND on the sheet: {x_scan_cmp656_bits_0_3_pin9[0], x_scan_cmp656_bits_0_3_pin9[1], x_scan_cmp656_bits_0_3_pin9[2], x_scan_cmp656_bits_0_3_pin9[3], x_scan_cmp656_bits_0_3_pin9[5], x_scan_cmp656_bits_0_3_pin9[6], x_scan_cmp656_bits_0_3_pin9[8], x_scan_cmp656_bits_0_3_pin9[10], x_scan_cmp656_bits_0_3_pin9[11], x_scan_cmp753_bits_0_3_pin9[1], x_scan_cmp753_bits_0_3_pin9[2], x_scan_cmp753_bits_0_3_pin9[3], x_scan_cmp753_bits_0_3_pin9[8], x_scan_cmp753_bits_0_3_pin9[10], x_scan_cmp753_bits_0_3_pin9[11], x_scan_cmp800_bits_0_3_pin9[0], x_scan_cmp800_bits_0_3_pin9[1], x_scan_cmp800_bits_0_3_pin9[2], x_scan_cmp800_bits_0_3_pin9[3], x_scan_cmp800_bits_0_3_pin9[4], x_scan_cmp800_bits_0_3_pin9[6], x_scan_cmp800_bits_0_3_pin9[7], x_scan_cmp800_bits_0_3_pin9[10], x_scan_cmp800_bits_0_3_pin9[11], x_scan_cmp656_bits_0_3_pin2[0], x_scan_cmp656_bits_0_3_pin2[2], x_scan_cmp753_bits_0_3_pin2[0], x_scan_cmp753_bits_0_3_pin2[2], x_scan_cmp800_bits_0_3_pin2[0], x_scan_cmp800_bits_0_3_pin2[2]}
  // also tied to VCC on the sheet: {x_scan_cmp656_bits_0_3_pin9[4], x_scan_cmp656_bits_0_3_pin9[7], x_scan_cmp656_bits_0_3_pin9[9], x_scan_cmp753_bits_0_3_pin9[0], x_scan_cmp753_bits_0_3_pin9[4], x_scan_cmp753_bits_0_3_pin9[5], x_scan_cmp753_bits_0_3_pin9[6], x_scan_cmp753_bits_0_3_pin9[7], x_scan_cmp753_bits_0_3_pin9[9], x_scan_cmp800_bits_0_3_pin9[5], x_scan_cmp800_bits_0_3_pin9[8], x_scan_cmp800_bits_0_3_pin9[9], x_scan_cmp656_bits_0_3_pin2[1], x_scan_cmp753_bits_0_3_pin2[1], x_scan_cmp800_bits_0_3_pin2[1]}

  // Notes on the sheet:
  //   X_Paddle
  //   HSYNC_START = 656
  //   10 bit: 1010010000
  //   656 stored as a 12-bit constant: 0010 1001 0000
  //   HSYNC_END = 753
  //   10 bit: 1011110001
  //   753 stored as a 12-bit constant: 0010 1111 0001
  //   LINE_END = 800
  //   12 bit: 0011 0010 0000
  //   X_SCAN COUNTER (10 bit usati)
  //   X_SCAN vs HSYNC_START
  //   X_SCAN vs HSYNC_END
  //   X_SCAN vs LINE_END
endmodule
