// Digital circuit c1_xy_scan_vga_test_4_6_8_paddle_window_stable.dig as structural Verilog
module c1_xy_scan_vga_test_4_6_8_paddle_window_stable (
  input  paddle_down,
  input  paddle_up,
  input  paddle_load_n,
  input  paddle_clear,
  input  paddle_q2_in,
  input  paddle_q3_in,
  input  paddle_q1_in,
  input  paddle_q0_in,
  input  pixel_clock,
  output paddle_d0,
  output paddle_d1,
  output paddle_d2,
  output paddle_d3,
  output paddle_borrow_out,
  output paddle_carry_out,
  output x_scan_b0,
  output x_scan_b1,
  output x_scan_b2,
  output x_scan_b3,
  output x_scan_b4,
  output x_scan_b5,
  output x_scan_b6,
  output x_scan_b7,
  output x_scan_b8,
  output x_scan_b9,
  output x_scan_gt_4,
  output x_scan_eq_4,
  output x_scan_lt_4,
  output x_scan_gt_6,
  output x_scan_eq_6,
  output x_scan_lt_6,
  output hsync_n,
  output x_scan_gt_8,
  output x_scan_eq_8,
  output x_scan_lt_8,
  output x_scan_clear_n,
  output y_scan_b0,
  output y_scan_b1,
  output y_scan_b2,
  output y_scan_b3,
  output y_scan_b4,
  output y_scan_b5,
  output y_scan_b6,
  output y_scan_b7,
  output y_scan_b8,
  output y_scan_b9,
  output y_scan_gt_4,
  output y_scan_eq_4,
  output y_scan_lt_4,
  output y_scan_gt_6,
  output y_scan_eq_6,
  output y_scan_lt_6,
  output vsync_n,
  output y_scan_gt_8,
  output y_scan_eq_8,
  output y_scan_lt_8,
  output y_scan_clear_n,
  output x_paddle_px_b0,
  output x_paddle_px_b1,
  output x_paddle_px_b2,
  output x_paddle_px_b3,
  output x_paddle_px_b4,
  output x_paddle_px_b5,
  output x_paddle_px_b6,
  output x_paddle_px_b7,
  output x_paddle_px_b8,
  output x_paddle_px_b9,
  output x_scan_gt_paddle_left,
  output x_scan_lt_paddle_right
);

  wire cmp_xscan_vs_paddle_left_CASCADE_0_EQ, cmp_xscan_vs_paddle_left_CASCADE_1_EQ,
       cmp_xscan_vs_paddle_left_CASCADE_1_GT, cmp_xscan_vs_paddle_left_CASCADE_1_LT,
       cmp_xscan_vs_paddle_right_CASCADE_0_EQ, cmp_xscan_vs_paddle_right_CASCADE_1_EQ,
       cmp_xscan_vs_paddle_right_CASCADE_1_GT, cmp_xscan_vs_paddle_right_CASCADE_1_LT, PWIDTH40_B0,
       PWIDTH40_B1, PWIDTH40_B2, PWIDTH40_B3, PWIDTH40_B4, PWIDTH40_B5, PWIDTH40_B6, PWIDTH40_B7,
       PWIDTH40_B8, PWIDTH40_B9, PWIDTH40_B10, PWIDTH40_B11, x_paddle_times_40_adder_pin1,
       x_paddle_times_40_adder_pin2, x_paddle_times_40_adder_pin3, x_paddle_times_40_adder_pin4,
       x_paddle_times_40_adder_pin5, x_paddle_times_40_adder_pin6, x_paddle_times_40_adder_pin7,
       x_paddle_times_40_adder_pin9, x_paddle_times_40_adder_pin10, x_paddle_times_40_adder_pin11,
       x_paddle_times_40_adder_pin12, x_paddle_times_40_adder_pin13, x_paddle_times_40_adder_pin14,
       x_paddle_times_40_adder_pin15, x_scan_cmp4_bits_0_3_pin2, x_scan_cmp4_bits_0_3_pin4,
       x_scan_cmp6_bits_0_3_pin2, x_scan_cmp6_bits_0_3_pin4, x_scan_cmp8_bits_0_3_pin2,
       x_scan_cmp8_bits_0_3_pin4, XP40_PLUS40_CARRY_0, XP40_PLUS40_CARRY_1, XP40_RIGHT_B0, XP40_RIGHT_B1,
       XP40_RIGHT_B2, XP40_RIGHT_B3, XP40_RIGHT_B4, XP40_RIGHT_B5, XP40_RIGHT_B6, XP40_RIGHT_B7,
       XP40_RIGHT_B8, XP40_RIGHT_B9, XP40_RIGHT_B10, XP40_RIGHT_B11, XSCAN_B0, XSCAN_B1, XSCAN_B2, XSCAN_B3,
       XSCAN_B4, XSCAN_B5, XSCAN_B6, XSCAN_B7, XSCAN_B8, XSCAN_B9, XSCAN_B10, XSCAN_B11,
       y_scan_cmp4_bits_0_3_pin2, y_scan_cmp4_bits_0_3_pin4, y_scan_cmp6_bits_0_3_pin2,
       y_scan_cmp6_bits_0_3_pin4, y_scan_cmp8_bits_0_3_pin2, y_scan_cmp8_bits_0_3_pin4;
  wire [1:0] cmp_xscan_vs_paddle_left_bits_0_3_pin2, cmp_xscan_vs_paddle_right_bits_0_3_pin2;

  _74193 x_paddle_counter (
    .pin1(paddle_load_n), .pin2(paddle_d2), .pin3(paddle_d3), .pin4(paddle_down), .pin5(paddle_up),
    .pin6(paddle_d1), .pin7(paddle_d0), .pin8(1'b0), .pin9(paddle_q3_in), .pin10(paddle_q2_in),
    .pin11(paddle_q1_in), .pin12(paddle_borrow_out), .pin13(paddle_carry_out), .pin14(paddle_q0_in),
    .pin15(paddle_clear), .pin16(1'b1));
  _74283 x_paddle_times_40_adder (
    .pin1(x_paddle_times_40_adder_pin1), .pin2(x_paddle_times_40_adder_pin2),
    .pin3(x_paddle_times_40_adder_pin3), .pin4(x_paddle_times_40_adder_pin4),
    .pin5(x_paddle_times_40_adder_pin5), .pin6(x_paddle_times_40_adder_pin6),
    .pin7(x_paddle_times_40_adder_pin7), .pin8(1'b0), .pin9(x_paddle_times_40_adder_pin9),
    .pin10(x_paddle_times_40_adder_pin10), .pin11(x_paddle_times_40_adder_pin11),
    .pin12(x_paddle_times_40_adder_pin12), .pin13(x_paddle_times_40_adder_pin13),
    .pin14(x_paddle_times_40_adder_pin14), .pin15(x_paddle_times_40_adder_pin15), .pin16(1'b1));
  _74163 x_scan_counter_bits_0_3 (
    .pin1(1'b1), .pin3(1'b0), .pin4(1'b0), .pin5(1'b0), .pin6(1'b0), .pin7(1'b1), .pin8(1'b0), .pin9(1'b1),
    .pin10(1'b1), .pin11(1'b0), .pin12(1'b0), .pin13(1'b0), .pin14(1'b0), .pin16(1'b1));  // open: pin2, pin15
  _74163 y_scan_counter_bits_0_3 (
    .pin1(y_scan_lt_8), .pin3(1'b0), .pin4(1'b0), .pin5(1'b0), .pin6(1'b0), .pin7(1'b1), .pin8(1'b0),
    .pin9(1'b1), .pin10(1'b1), .pin11(1'b0), .pin12(1'b0), .pin13(1'b0), .pin14(1'b0), .pin16(1'b1));  // open: pin2, pin15
  _7485 x_scan_cmp4_bits_0_3 (
    .pin2(x_scan_cmp4_bits_0_3_pin2), .pin4(x_scan_cmp4_bits_0_3_pin4), .pin5(1'b0), .pin8(1'b0),
    .pin10(1'b0), .pin12(1'b0), .pin13(1'b0), .pin15(1'b0));  // open: pin1, pin3, pin6, pin7, pin9, pin11, pin14, pin16
  _7485 x_scan_cmp6_bits_0_3 (
    .pin2(x_scan_cmp6_bits_0_3_pin2), .pin4(x_scan_cmp6_bits_0_3_pin4), .pin5(1'b0), .pin8(1'b0),
    .pin10(1'b0), .pin12(1'b0), .pin13(1'b0), .pin15(1'b0));  // open: pin1, pin3, pin6, pin7, pin9, pin11, pin14, pin16
  _7485 x_scan_cmp8_bits_0_3 (
    .pin2(x_scan_cmp8_bits_0_3_pin2), .pin4(x_scan_cmp8_bits_0_3_pin4), .pin5(1'b0), .pin7(1'b0),
    .pin8(1'b0), .pin10(1'b0), .pin12(1'b0), .pin13(1'b0), .pin15(1'b0));  // open: pin1, pin3, pin6, pin9, pin11, pin14, pin16
  _7485 y_scan_cmp4_bits_0_3 (
    .pin2(y_scan_cmp4_bits_0_3_pin2), .pin4(y_scan_cmp4_bits_0_3_pin4), .pin5(1'b0), .pin8(1'b0),
    .pin10(1'b0), .pin12(1'b0), .pin13(1'b0), .pin15(1'b0));  // open: pin1, pin3, pin6, pin7, pin9, pin11, pin14, pin16
  _7485 y_scan_cmp6_bits_0_3 (
    .pin2(y_scan_cmp6_bits_0_3_pin2), .pin4(y_scan_cmp6_bits_0_3_pin4), .pin5(1'b0), .pin8(1'b0),
    .pin10(1'b0), .pin12(1'b0), .pin13(1'b0), .pin15(1'b0));  // open: pin1, pin3, pin6, pin7, pin9, pin11, pin14, pin16
  _7485 y_scan_cmp8_bits_0_3 (
    .pin2(y_scan_cmp8_bits_0_3_pin2), .pin4(y_scan_cmp8_bits_0_3_pin4), .pin5(1'b0), .pin7(1'b0),
    .pin8(1'b0), .pin10(1'b0), .pin12(1'b0), .pin13(1'b0), .pin15(1'b0));  // open: pin1, pin3, pin6, pin9, pin11, pin14, pin16
  _74163 x_scan_counter_bits_4_7 (
    .pin1(1'b1), .pin3(1'b0), .pin4(1'b0), .pin5(1'b0), .pin6(1'b0), .pin8(1'b0), .pin9(pixel_clock),
    .pin10(pixel_clock), .pin11(1'b0), .pin12(1'b0), .pin13(1'b0), .pin14(1'b0), .pin16(pixel_clock));  // open: pin2, pin7, pin15
  _74163 y_scan_counter_bits_4_7 (
    .pin1(y_scan_lt_8), .pin3(1'b0), .pin4(1'b0), .pin5(1'b0), .pin6(1'b0), .pin8(1'b0), .pin9(1'b1),
    .pin10(1'b1), .pin11(1'b0), .pin12(1'b0), .pin13(1'b0), .pin14(1'b0), .pin16(1'b1));  // open: pin2, pin7, pin15
  // _7485 x_scan_cmp4_bits_4_7: pin names not known; wires that end beside it: 1'b0, 1'b0, 1'b0, 1'b0, 1'b0, 1'b0, 1'b1, 1'b1
  // _7485 x_scan_cmp6_bits_4_7: pin names not known; wires that end beside it: 1'b0, 1'b0, 1'b0, 1'b0, 1'b0, 1'b0, 1'b0, 1'b0, 1'b1, 1'b1
  // _7485 x_scan_cmp8_bits_4_7: pin names not known; wires that end beside it: 1'b0, 1'b0, 1'b0, 1'b0, 1'b0, 1'b0, 1'b0, 1'b0, 1'b1, 1'b1
  // _7485 y_scan_cmp4_bits_4_7: pin names not known; wires that end beside it: 1'b0, 1'b0, 1'b0, 1'b0, 1'b0, 1'b0, 1'b1, 1'b1
  // _7485 y_scan_cmp6_bits_4_7: pin names not known; wires that end beside it: 1'b0, 1'b0, 1'b0, 1'b0, 1'b0, 1'b0, 1'b0, 1'b0, 1'b1, 1'b1
  // _7485 y_scan_cmp8_bits_4_7: pin names not known; wires that end beside it: 1'b0, 1'b0, 1'b0, 1'b0, 1'b0, 1'b0, 1'b0, 1'b0, 1'b1, 1'b1
  _74163 x_scan_counter_bits_8_11 (
    .pin1(1'b1), .pin2(pixel_clock), .pin3(1'b0), .pin4(1'b0), .pin5(1'b0), .pin6(1'b0), .pin8(1'b0),
    .pin9(pixel_clock), .pin10(pixel_clock), .pin11(x_scan_b8), .pin12(x_scan_b8), .pin13(x_scan_b8),
    .pin14(x_scan_b8), .pin16(pixel_clock));  // open: pin7, pin15
  _74163 y_scan_counter_bits_8_11 (
    .pin1(y_scan_lt_8), .pin2(1'b1), .pin3(1'b0), .pin4(1'b0), .pin5(1'b0), .pin6(1'b0), .pin8(1'b0),
    .pin9(1'b1), .pin10(1'b1), .pin11(y_scan_b8), .pin12(y_scan_b8), .pin13(y_scan_b8), .pin14(y_scan_b8),
    .pin16(1'b1));  // open: pin7, pin15
  _7485 x_scan_cmp4_bits_8_11 (
    .pin1(1'b1), .pin2(1'b0), .pin4(1'b0), .pin5(x_scan_gt_4), .pin6(1'b0), .pin7(x_scan_lt_4), .pin8(1'b0),
    .pin9(1'b0), .pin10(x_scan_b8), .pin11(1'b0), .pin12(x_scan_b8), .pin13(x_scan_b8), .pin14(1'b0),
    .pin15(x_scan_b8), .pin16(1'b1));  // open: pin3
  _7485 x_scan_cmp6_bits_8_11 (
    .pin1(1'b1), .pin2(1'b0), .pin4(1'b0), .pin5(x_scan_gt_6), .pin6(1'b0), .pin7(x_scan_lt_6), .pin8(1'b0),
    .pin9(1'b0), .pin10(x_scan_b8), .pin11(1'b0), .pin12(x_scan_b8), .pin13(x_scan_b8), .pin14(1'b0),
    .pin15(x_scan_b8), .pin16(1'b1));  // open: pin3
  _7485 x_scan_cmp8_bits_8_11 (
    .pin1(1'b1), .pin2(1'b0), .pin4(1'b0), .pin5(x_scan_gt_8), .pin6(1'b0), .pin7(1'b1), .pin8(1'b0),
    .pin9(1'b0), .pin10(x_scan_b8), .pin11(1'b0), .pin12(x_scan_b8), .pin13(x_scan_b8), .pin14(1'b0),
    .pin15(x_scan_b8), .pin16(1'b1));  // open: pin3
  _7485 y_scan_cmp4_bits_8_11 (
    .pin1(1'b1), .pin2(1'b0), .pin4(1'b0), .pin5(y_scan_gt_4), .pin6(1'b0), .pin7(y_scan_lt_4), .pin8(1'b0),
    .pin9(1'b0), .pin10(y_scan_b8), .pin11(1'b0), .pin12(y_scan_b8), .pin13(y_scan_b8), .pin14(1'b0),
    .pin15(y_scan_b8), .pin16(1'b1));  // open: pin3
  _7485 y_scan_cmp6_bits_8_11 (
    .pin1(1'b1), .pin2(1'b0), .pin4(1'b0), .pin5(y_scan_gt_6), .pin6(1'b0), .pin7(y_scan_lt_6), .pin8(1'b0),
    .pin9(1'b0), .pin10(y_scan_b8), .pin11(1'b0), .pin12(y_scan_b8), .pin13(y_scan_b8), .pin14(1'b0),
    .pin15(y_scan_b8), .pin16(1'b1));  // open: pin3
  _7485 y_scan_cmp8_bits_8_11 (
    .pin1(1'b1), .pin2(1'b0), .pin4(1'b0), .pin5(y_scan_gt_8), .pin6(1'b0), .pin7(y_scan_lt_8), .pin8(1'b0),
    .pin9(1'b0), .pin10(y_scan_b8), .pin11(1'b0), .pin12(y_scan_b8), .pin13(y_scan_b8), .pin14(1'b0),
    .pin15(y_scan_b8), .pin16(1'b1));  // open: pin3
  // NAnd x_test_window_nand is placed but not wired
  // NAnd y_test_window_nand is placed but not wired
  _74283 x_paddle_plus40_bits_0_3 (
    .pin1(XP40_RIGHT_B1), .pin2(PWIDTH40_B1), .pin3(1'b0), .pin4(XP40_RIGHT_B0), .pin5(1'b0),
    .pin6(PWIDTH40_B0), .pin7(1'b0), .pin8(1'b0), .pin9(XP40_PLUS40_CARRY_0), .pin10(XP40_RIGHT_B3),
    .pin11(PWIDTH40_B3), .pin12(x_paddle_px_b3), .pin13(XP40_RIGHT_B2), .pin14(1'b0), .pin15(PWIDTH40_B2),
    .pin16(1'b1));
  _7485 cmp_xscan_vs_paddle_left_bits_0_3 (
    .pin1(x_paddle_px_b3), .pin2(cmp_xscan_vs_paddle_left_bits_0_3_pin2[0]),
    .pin3(cmp_xscan_vs_paddle_left_bits_0_3_pin2[1]), .pin4(cmp_xscan_vs_paddle_left_CASCADE_0_EQ),
    .pin5(cmp_xscan_vs_paddle_left_CASCADE_0_EQ), .pin6(cmp_xscan_vs_paddle_left_CASCADE_0_EQ),
    .pin7(cmp_xscan_vs_paddle_left_CASCADE_0_EQ), .pin8(1'b0), .pin9(1'b0), .pin10(XSCAN_B0), .pin11(1'b0),
    .pin12(XSCAN_B1), .pin13(XSCAN_B2), .pin14(1'b0), .pin15(XSCAN_B3), .pin16(1'b1));
  _7485 cmp_xscan_vs_paddle_right_bits_0_3 (
    .pin1(XP40_RIGHT_B3), .pin2(cmp_xscan_vs_paddle_right_bits_0_3_pin2[0]),
    .pin3(cmp_xscan_vs_paddle_right_bits_0_3_pin2[1]), .pin4(cmp_xscan_vs_paddle_right_CASCADE_0_EQ),
    .pin5(cmp_xscan_vs_paddle_right_CASCADE_0_EQ), .pin6(cmp_xscan_vs_paddle_right_CASCADE_0_EQ),
    .pin7(cmp_xscan_vs_paddle_right_CASCADE_0_EQ), .pin8(1'b0), .pin9(XP40_RIGHT_B0), .pin10(XSCAN_B0),
    .pin11(XP40_RIGHT_B1), .pin12(XSCAN_B1), .pin13(XSCAN_B2), .pin14(XP40_RIGHT_B2), .pin15(XSCAN_B3),
    .pin16(1'b1));
  _74283 x_paddle_plus40_bits_4_7 (
    .pin1(XP40_RIGHT_B5), .pin2(PWIDTH40_B5), .pin3(x_paddle_px_b5), .pin4(XP40_RIGHT_B4),
    .pin5(x_paddle_px_b4), .pin6(PWIDTH40_B4), .pin7(XP40_PLUS40_CARRY_0), .pin8(1'b0),
    .pin9(XP40_PLUS40_CARRY_1), .pin10(XP40_RIGHT_B7), .pin11(PWIDTH40_B7), .pin12(x_paddle_px_b7),
    .pin13(XP40_RIGHT_B6), .pin14(x_paddle_px_b6), .pin15(PWIDTH40_B6), .pin16(1'b1));
  _7485 cmp_xscan_vs_paddle_left_bits_4_7 (
    .pin1(x_paddle_px_b7), .pin2(cmp_xscan_vs_paddle_left_CASCADE_0_EQ),
    .pin3(cmp_xscan_vs_paddle_left_CASCADE_0_EQ), .pin4(cmp_xscan_vs_paddle_left_CASCADE_0_EQ),
    .pin5(cmp_xscan_vs_paddle_left_CASCADE_1_GT), .pin6(cmp_xscan_vs_paddle_left_CASCADE_1_EQ),
    .pin7(cmp_xscan_vs_paddle_left_CASCADE_1_LT), .pin8(1'b0), .pin9(x_paddle_px_b4), .pin10(XSCAN_B4),
    .pin11(x_paddle_px_b5), .pin12(XSCAN_B5), .pin13(XSCAN_B6), .pin14(x_paddle_px_b6), .pin15(XSCAN_B7),
    .pin16(1'b1));
  _7485 cmp_xscan_vs_paddle_right_bits_4_7 (
    .pin1(XP40_RIGHT_B7), .pin2(cmp_xscan_vs_paddle_right_CASCADE_0_EQ),
    .pin3(cmp_xscan_vs_paddle_right_CASCADE_0_EQ), .pin4(cmp_xscan_vs_paddle_right_CASCADE_0_EQ),
    .pin5(cmp_xscan_vs_paddle_right_CASCADE_1_GT), .pin6(cmp_xscan_vs_paddle_right_CASCADE_1_EQ),
    .pin7(cmp_xscan_vs_paddle_right_CASCADE_1_LT), .pin8(1'b0), .pin9(XP40_RIGHT_B4), .pin10(XSCAN_B4),
    .pin11(XP40_RIGHT_B5), .pin12(XSCAN_B5), .pin13(XSCAN_B6), .pin14(XP40_RIGHT_B6), .pin15(XSCAN_B7),
    .pin16(1'b1));
  _74283 x_paddle_plus40_bits_8_11 (
    .pin1(XP40_RIGHT_B9), .pin2(PWIDTH40_B9), .pin3(x_paddle_px_b9), .pin4(XP40_RIGHT_B8),
    .pin5(x_paddle_px_b8), .pin6(PWIDTH40_B8), .pin7(XP40_PLUS40_CARRY_1), .pin8(1'b0),
    .pin10(XP40_RIGHT_B11), .pin11(PWIDTH40_B11), .pin12(1'b0), .pin13(XP40_RIGHT_B10), .pin14(1'b0),
    .pin15(PWIDTH40_B10), .pin16(1'b1));  // open: pin9
  _7485 cmp_xscan_vs_paddle_left_bits_8_11 (
    .pin1(1'b0), .pin2(cmp_xscan_vs_paddle_left_CASCADE_1_LT), .pin3(cmp_xscan_vs_paddle_left_CASCADE_1_EQ),
    .pin4(cmp_xscan_vs_paddle_left_CASCADE_1_GT), .pin5(x_scan_gt_paddle_left), .pin8(1'b0),
    .pin9(x_paddle_px_b8), .pin10(XSCAN_B8), .pin11(x_paddle_px_b9), .pin13(XSCAN_B10), .pin14(1'b0),
    .pin15(XSCAN_B11), .pin16(1'b1));  // open: pin6, pin7, pin12
  _7485 cmp_xscan_vs_paddle_right_bits_8_11 (
    .pin1(XP40_RIGHT_B11), .pin2(cmp_xscan_vs_paddle_right_CASCADE_1_LT),
    .pin3(cmp_xscan_vs_paddle_right_CASCADE_1_EQ), .pin4(cmp_xscan_vs_paddle_right_CASCADE_1_GT),
    .pin7(x_scan_lt_paddle_right), .pin8(1'b0), .pin9(XP40_RIGHT_B8), .pin11(XP40_RIGHT_B9),
    .pin12(XSCAN_B9), .pin13(XSCAN_B10), .pin14(XP40_RIGHT_B10), .pin15(XSCAN_B11), .pin16(1'b1));  // open: pin5, pin6, pin10
  // And paddle_x_window_and has open pins: In_1=x_scan_gt_paddle_left, In_2=x_scan_lt_paddle_right, out=open

  assign x_paddle_px_b0 = 1'b0;
  assign x_paddle_px_b1 = 1'b0;
  assign x_paddle_px_b2 = 1'b0;
  assign x_scan_b0 = 1'b0;
  assign x_scan_b1 = 1'b0;
  assign x_scan_b2 = 1'b0;
  assign x_scan_b3 = 1'b0;
  assign x_scan_b4 = 1'b0;
  assign x_scan_b5 = 1'b0;
  assign x_scan_b6 = 1'b0;
  assign x_scan_b7 = 1'b0;
  assign x_scan_b9 = x_scan_b8;
  assign x_scan_eq_4 = 1'b0;
  assign x_scan_eq_6 = 1'b0;
  assign x_scan_eq_8 = 1'b0;
  assign x_scan_lt_8 = 1'b1;
  assign y_scan_b0 = 1'b0;
  assign y_scan_b1 = 1'b0;
  assign y_scan_b2 = 1'b0;
  assign y_scan_b3 = 1'b0;
  assign y_scan_b4 = 1'b0;
  assign y_scan_b5 = 1'b0;
  assign y_scan_b6 = 1'b0;
  assign y_scan_b7 = 1'b0;
  assign y_scan_b9 = y_scan_b8;
  assign y_scan_eq_4 = 1'b0;
  assign y_scan_eq_6 = 1'b0;
  assign y_scan_eq_8 = 1'b0;
  // also tied to GND on the sheet: {PWIDTH40_B0, PWIDTH40_B1, PWIDTH40_B2, PWIDTH40_B4, PWIDTH40_B6, PWIDTH40_B7, PWIDTH40_B8, PWIDTH40_B9, PWIDTH40_B10, PWIDTH40_B11, cmp_xscan_vs_paddle_left_bits_0_3_pin2[0], cmp_xscan_vs_paddle_left_CASCADE_0_EQ, cmp_xscan_vs_paddle_right_bits_0_3_pin2[0], cmp_xscan_vs_paddle_right_CASCADE_0_EQ}
  // also tied to VCC on the sheet: {PWIDTH40_B3, PWIDTH40_B5, cmp_xscan_vs_paddle_left_bits_0_3_pin2[1], cmp_xscan_vs_paddle_right_bits_0_3_pin2[1], pixel_clock}

  // Other names for the same wires on the sheet: cmp_xscan_vs_paddle_left_CASCADE_0_GT = cmp_xscan_vs_paddle_left_CASCADE_0_EQ;
  //   cmp_xscan_vs_paddle_left_CASCADE_0_LT = cmp_xscan_vs_paddle_left_CASCADE_0_EQ;
  //   cmp_xscan_vs_paddle_right_CASCADE_0_GT = cmp_xscan_vs_paddle_right_CASCADE_0_EQ;
  //   cmp_xscan_vs_paddle_right_CASCADE_0_LT = cmp_xscan_vs_paddle_right_CASCADE_0_EQ; PADDLE_Q0 = x_paddle_px_b3;
  //   PADDLE_Q1 = x_paddle_px_b4; XP40_B5 = x_paddle_px_b5; XP40_B6 = x_paddle_px_b6; XP40_B7 = x_paddle_px_b7;
  //   XP40_B8 = x_paddle_px_b8; XP40_B9 = x_paddle_px_b9

  // Notes on the sheet:
  //   X_Paddle
  //   PADDLE X × 40
  //   40·X = (X << 5) + (X << 3)
  //   uscita: 0, 40, 80, …, 600
  //   x_paddle_px[9:0]
  //   TEST_START = 4
  //   10 bit: 0000000100
  //   4 stored as a 12-bit constant: 0000 0000 0100
  //   TEST_END = 6
  //   10 bit: 0000000110
  //   6 stored as a 12-bit constant: 0000 0000 0110
  //   TEST_LINE_END = 8
  //   12 bit: 0000 0000 1000
  //   Y clock: fronte di salita di x_scan_lt_8 (una volta per riga di prova)
  //   TEST_FRAME_END = 8
  //   X_SCAN COUNTER (10 bit usati)
  //   Y_SCAN COUNTER (10 bit usati)
  //   X_SCAN vs TEST_START
  //   X_SCAN vs TEST_END
  //   X_SCAN vs TEST_LINE_END
  //   Y_SCAN vs TEST_START
  //   Y_SCAN vs TEST_END
  //   Y_SCAN vs TEST_FRAME_END
  //   PADDLE RIGHT EDGE = X_paddle_px + 40
  //   12-bit addition
  //   X_SCAN > X_PADDLE_LEFT
  //   X_SCAN < X_PADDLE_RIGHT (= LEFT + 40)
  //   PADDLE HORIZONTAL WINDOW
endmodule
