// Digital circuit c1_xy_scan_vga_test_4_6_8_paddle_window_tunnels_fixed.dig as structural Verilog
module c1_xy_scan_vga_test_4_6_8_paddle_window_tunnels_fixed (
  input  paddle_down,
  input  paddle_up,
  input  paddle_load_n,
  input  paddle_clear,
  input  paddle_q2_in,
  input  paddle_q3_in,
  input  paddle_q1_in,
  input  paddle_q0_in,
  input  pixel_clock,
  output paddle_d0,
  output paddle_d1,
  output paddle_d2,
  output paddle_d3,
  output paddle_borrow_out,
  output paddle_carry_out,
  output x_scan_b0,
  output x_scan_b1,
  output x_scan_b2,
  output x_scan_b3,
  output x_scan_b4,
  output x_scan_b5,
  output x_scan_b6,
  output x_scan_b7,
  output x_scan_b8,
  output x_scan_b9,
  output x_scan_gt_4,
  output x_scan_eq_4,
  output x_scan_lt_4,
  output x_scan_gt_6,
  output x_scan_eq_6,
  output x_scan_lt_6,
  output hsync_n,
  output x_scan_gt_8,
  output x_scan_eq_8,
  output x_scan_lt_8,
  output x_scan_clear_n,
  output y_scan_b0,
  output y_scan_b1,
  output y_scan_b2,
  output y_scan_b3,
  output y_scan_b4,
  output y_scan_b5,
  output y_scan_b6,
  output y_scan_b7,
  output y_scan_b8,
  output y_scan_b9,
  output y_scan_gt_4,
  output y_scan_eq_4,
  output y_scan_lt_4,
  output y_scan_gt_6,
  output y_scan_eq_6,
  output y_scan_lt_6,
  output vsync_n,
  output y_scan_gt_8,
  output y_scan_eq_8,
  output y_scan_lt_8,
  output y_scan_clear_n,
  output x_paddle_px_b0,
  output x_paddle_px_b1,
  output x_paddle_px_b2,
  output x_paddle_px_b3,
  output x_paddle_px_b4,
  output x_paddle_px_b5,
  output x_paddle_px_b6,
  output x_paddle_px_b7,
  output x_paddle_px_b8,
  output x_paddle_px_b9,
  output x_paddle_right_b0,
  output x_paddle_right_b1,
  output x_paddle_right_b2,
  output x_paddle_right_b3,
  output x_paddle_right_b4,
  output x_paddle_right_b5,
  output x_paddle_right_b6,
  output x_paddle_right_b7,
  output x_paddle_right_b8,
  output x_paddle_right_b9,
  output paddle_x_visible,
  output x_scan_gt_paddle_left,
  output x_scan_lt_paddle_right
);

  wire cmp_xscan_vs_paddle_left_CASCADE_0_EQ, cmp_xscan_vs_paddle_left_CASCADE_0_GT,
       cmp_xscan_vs_paddle_left_CASCADE_0_LT, cmp_xscan_vs_paddle_left_CASCADE_1_EQ,
       cmp_xscan_vs_paddle_left_CASCADE_1_GT, cmp_xscan_vs_paddle_left_CASCADE_1_LT,
       cmp_xscan_vs_paddle_left_EQ, cmp_xscan_vs_paddle_left_LT, cmp_xscan_vs_paddle_right_CASCADE_0_EQ,
       cmp_xscan_vs_paddle_right_CASCADE_0_GT, cmp_xscan_vs_paddle_right_CASCADE_0_LT,
       cmp_xscan_vs_paddle_right_CASCADE_1_EQ, cmp_xscan_vs_paddle_right_CASCADE_1_GT,
       cmp_xscan_vs_paddle_right_CASCADE_1_LT, cmp_xscan_vs_paddle_right_EQ, cmp_xscan_vs_paddle_right_GT,
       PWIDTH40_B0, PWIDTH40_B1, PWIDTH40_B2, PWIDTH40_B3, PWIDTH40_B4, PWIDTH40_B5, PWIDTH40_B6,
       PWIDTH40_B7, PWIDTH40_B8, PWIDTH40_B9, PWIDTH40_B10, PWIDTH40_B11, x_scan_cmp4_bits_0_3_pin5,
       x_scan_cmp4_bits_0_3_pin6, x_scan_cmp4_bits_0_3_pin7, x_scan_cmp4_bits_4_7_pin5,
       x_scan_cmp4_bits_4_7_pin6, x_scan_cmp4_bits_4_7_pin7, x_scan_cmp6_bits_0_3_pin5,
       x_scan_cmp6_bits_0_3_pin6, x_scan_cmp6_bits_0_3_pin7, x_scan_cmp6_bits_4_7_pin5,
       x_scan_cmp6_bits_4_7_pin6, x_scan_cmp6_bits_4_7_pin7, x_scan_cmp8_bits_0_3_pin5,
       x_scan_cmp8_bits_0_3_pin6, x_scan_cmp8_bits_0_3_pin7, x_scan_cmp8_bits_4_7_pin5,
       x_scan_cmp8_bits_4_7_pin6, x_scan_cmp8_bits_4_7_pin7, x_scan_counter_bits_0_3_pin15,
       x_scan_counter_bits_4_7_pin15, XP40_PLUS40_CARRY_0, XP40_PLUS40_CARRY_1, XP40_RIGHT_B10,
       XP40_RIGHT_B11, XSCAN_B10, XSCAN_B11, y_scan_cmp4_bits_0_3_pin5, y_scan_cmp4_bits_0_3_pin6,
       y_scan_cmp4_bits_0_3_pin7, y_scan_cmp4_bits_4_7_pin5, y_scan_cmp4_bits_4_7_pin6,
       y_scan_cmp4_bits_4_7_pin7, y_scan_cmp6_bits_0_3_pin5, y_scan_cmp6_bits_0_3_pin6,
       y_scan_cmp6_bits_0_3_pin7, y_scan_cmp6_bits_4_7_pin5, y_scan_cmp6_bits_4_7_pin6,
       y_scan_cmp6_bits_4_7_pin7, y_scan_cmp8_bits_0_3_pin5, y_scan_cmp8_bits_0_3_pin6,
       y_scan_cmp8_bits_0_3_pin7, y_scan_cmp8_bits_4_7_pin5, y_scan_cmp8_bits_4_7_pin6,
       y_scan_cmp8_bits_4_7_pin7, y_scan_counter_bits_0_3_pin15, y_scan_counter_bits_4_7_pin15,
       y_scan_counter_bits_8_11_pin11, y_scan_counter_bits_8_11_pin12;
  wire [2:0] cmp_xscan_vs_paddle_left_bits_0_3_pin2, cmp_xscan_vs_paddle_right_bits_0_3_pin2,
       x_scan_cmp4_bits_0_3_pin2, x_scan_cmp6_bits_0_3_pin2, x_scan_cmp8_bits_0_3_pin2,
       y_scan_cmp4_bits_0_3_pin2, y_scan_cmp6_bits_0_3_pin2, y_scan_cmp8_bits_0_3_pin2;
  wire [11:0] x_scan_cmp4_bits_0_3_pin9, x_scan_cmp6_bits_0_3_pin9, x_scan_cmp8_bits_0_3_pin9,
       y_scan_cmp4_bits_0_3_pin9, y_scan_cmp6_bits_0_3_pin9, y_scan_cmp8_bits_0_3_pin9;

  _74193 x_paddle_counter (
    .pin1(paddle_load_n), .pin2(paddle_d2), .pin3(paddle_d3), .pin4(paddle_down), .pin5(paddle_up),
    .pin6(paddle_d1), .pin7(paddle_d0), .pin8(1'b0), .pin9(paddle_q3_in), .pin10(paddle_q2_in),
    .pin11(paddle_q1_in), .pin12(paddle_borrow_out), .pin13(paddle_carry_out), .pin14(paddle_q0_in),
    .pin15(paddle_clear), .pin16(1'b1));
  _74283 x_paddle_times_40_adder (
    .pin1(x_paddle_px_b6), .pin2(paddle_d0), .pin3(paddle_d2), .pin4(x_paddle_px_b5), .pin5(paddle_d3),
    .pin6(paddle_d1), .pin7(1'b0), .pin8(1'b0), .pin9(x_paddle_px_b9), .pin10(x_paddle_px_b8), .pin11(1'b0),
    .pin12(paddle_d0), .pin13(x_paddle_px_b7), .pin14(paddle_d1), .pin15(1'b0), .pin16(1'b1));
  _74163 x_scan_counter_bits_0_3 (
    .pin1(x_scan_clear_n), .pin2(pixel_clock), .pin3(1'b0), .pin4(1'b0), .pin5(1'b0), .pin6(1'b0),
    .pin7(1'b1), .pin8(1'b0), .pin9(1'b1), .pin10(1'b1), .pin11(x_scan_b3), .pin12(x_scan_b2),
    .pin13(x_scan_b1), .pin14(x_scan_b0), .pin15(x_scan_counter_bits_0_3_pin15), .pin16(1'b1));
  _74163 y_scan_counter_bits_0_3 (
    .pin1(y_scan_clear_n), .pin2(x_scan_clear_n), .pin3(1'b0), .pin4(1'b0), .pin5(1'b0), .pin6(1'b0),
    .pin7(1'b1), .pin8(1'b0), .pin9(1'b1), .pin10(1'b1), .pin11(y_scan_b3), .pin12(y_scan_b2),
    .pin13(y_scan_b1), .pin14(y_scan_b0), .pin15(y_scan_counter_bits_0_3_pin15), .pin16(1'b1));
  _7485 x_scan_cmp4_bits_0_3 (
    .pin1(x_scan_cmp4_bits_0_3_pin9[3]), .pin2(x_scan_cmp4_bits_0_3_pin2[0]),
    .pin3(x_scan_cmp4_bits_0_3_pin2[1]), .pin4(x_scan_cmp4_bits_0_3_pin2[2]),
    .pin5(x_scan_cmp4_bits_0_3_pin5), .pin6(x_scan_cmp4_bits_0_3_pin6), .pin7(x_scan_cmp4_bits_0_3_pin7),
    .pin8(1'b0), .pin9(x_scan_cmp4_bits_0_3_pin9[0]), .pin10(x_scan_b0),
    .pin11(x_scan_cmp4_bits_0_3_pin9[1]), .pin12(x_scan_b1), .pin13(x_scan_b2),
    .pin14(x_scan_cmp4_bits_0_3_pin9[2]), .pin15(x_scan_b3), .pin16(1'b1));
  _7485 x_scan_cmp6_bits_0_3 (
    .pin1(x_scan_cmp6_bits_0_3_pin9[3]), .pin2(x_scan_cmp6_bits_0_3_pin2[0]),
    .pin3(x_scan_cmp6_bits_0_3_pin2[1]), .pin4(x_scan_cmp6_bits_0_3_pin2[2]),
    .pin5(x_scan_cmp6_bits_0_3_pin5), .pin6(x_scan_cmp6_bits_0_3_pin6), .pin7(x_scan_cmp6_bits_0_3_pin7),
    .pin8(1'b0), .pin9(x_scan_cmp6_bits_0_3_pin9[0]), .pin10(x_scan_b0),
    .pin11(x_scan_cmp6_bits_0_3_pin9[1]), .pin12(x_scan_b1), .pin13(x_scan_b2),
    .pin14(x_scan_cmp6_bits_0_3_pin9[2]), .pin15(x_scan_b3), .pin16(1'b1));
  _7485 x_scan_cmp8_bits_0_3 (
    .pin1(x_scan_cmp8_bits_0_3_pin9[3]), .pin2(x_scan_cmp8_bits_0_3_pin2[0]),
    .pin3(x_scan_cmp8_bits_0_3_pin2[1]), .pin4(x_scan_cmp8_bits_0_3_pin2[2]),
    .pin5(x_scan_cmp8_bits_0_3_pin5), .pin6(x_scan_cmp8_bits_0_3_pin6), .pin7(x_scan_cmp8_bits_0_3_pin7),
    .pin8(1'b0), .pin9(x_scan_cmp8_bits_0_3_pin9[0]), .pin10(x_scan_b0),
    .pin11(x_scan_cmp8_bits_0_3_pin9[1]), .pin12(x_scan_b1), .pin13(x_scan_b2),
    .pin14(x_scan_cmp8_bits_0_3_pin9[2]), .pin15(x_scan_b3), .pin16(1'b1));
  _7485 y_scan_cmp4_bits_0_3 (
    .pin1(y_scan_cmp4_bits_0_3_pin9[3]), .pin2(y_scan_cmp4_bits_0_3_pin2[0]),
    .pin3(y_scan_cmp4_bits_0_3_pin2[1]), .pin4(y_scan_cmp4_bits_0_3_pin2[2]),
    .pin5(y_scan_cmp4_bits_0_3_pin5), .pin6(y_scan_cmp4_bits_0_3_pin6), .pin7(y_scan_cmp4_bits_0_3_pin7),
    .pin8(1'b0), .pin9(y_scan_cmp4_bits_0_3_pin9[0]), .pin10(y_scan_b0),
    .pin11(y_scan_cmp4_bits_0_3_pin9[1]), .pin12(y_scan_b1), .pin13(y_scan_b2),
    .pin14(y_scan_cmp4_bits_0_3_pin9[2]), .pin15(y_scan_b3), .pin16(1'b1));
  _7485 y_scan_cmp6_bits_0_3 (
    .pin1(y_scan_cmp6_bits_0_3_pin9[3]), .pin2(y_scan_cmp6_bits_0_3_pin2[0]),
    .pin3(y_scan_cmp6_bits_0_3_pin2[1]), .pin4(y_scan_cmp6_bits_0_3_pin2[2]),
    .pin5(y_scan_cmp6_bits_0_3_pin5), .pin6(y_scan_cmp6_bits_0_3_pin6), .pin7(y_scan_cmp6_bits_0_3_pin7),
    .pin8(1'b0), .pin9(y_scan_cmp6_bits_0_3_pin9[0]), .pin10(y_scan_b0),
    .pin11(y_scan_cmp6_bits_0_3_pin9[1]), .pin12(y_scan_b1), .pin13(y_scan_b2),
    .pin14(y_scan_cmp6_bits_0_3_pin9[2]), .pin15(y_scan_b3), .pin16(1'b1));
  _7485 y_scan_cmp8_bits_0_3 (
    .pin1(y_scan_cmp8_bits_0_3_pin9[3]), .pin2(y_scan_cmp8_bits_0_3_pin2[0]),
    .pin3(y_scan_cmp8_bits_0_3_pin2[1]), .pin4(y_scan_cmp8_bits_0_3_pin2[2]),
    .pin5(y_scan_cmp8_bits_0_3_pin5), .pin6(y_scan_cmp8_bits_0_3_pin6), .pin7(y_scan_cmp8_bits_0_3_pin7),
    .pin8(1'b0), .pin9(y_scan_cmp8_bits_0_3_pin9[0]), .pin10(y_scan_b0),
    .pin11(y_scan_cmp8_bits_0_3_pin9[1]), .pin12(y_scan_b1), .pin13(y_scan_b2),
    .pin14(y_scan_cmp8_bits_0_3_pin9[2]), .pin15(y_scan_b3), .pin16(1'b1));
  _74163 x_scan_counter_bits_4_7 (
    .pin1(x_scan_clear_n), .pin2(pixel_clock), .pin3(1'b0), .pin4(1'b0), .pin5(1'b0), .pin6(1'b0),
    .pin7(1'b1), .pin8(1'b0), .pin9(1'b1), .pin10(x_scan_counter_bits_0_3_pin15), .pin11(x_scan_b7),
    .pin12(x_scan_b6), .pin13(x_scan_b5), .pin14(x_scan_b4), .pin15(x_scan_counter_bits_4_7_pin15),
    .pin16(1'b1));
  _74163 y_scan_counter_bits_4_7 (
    .pin1(y_scan_clear_n), .pin2(x_scan_clear_n), .pin3(1'b0), .pin4(1'b0), .pin5(1'b0), .pin6(1'b0),
    .pin7(1'b1), .pin8(1'b0), .pin9(1'b1), .pin10(y_scan_counter_bits_0_3_pin15), .pin11(y_scan_b7),
    .pin12(y_scan_b6), .pin13(y_scan_b5), .pin14(y_scan_b4), .pin15(y_scan_counter_bits_4_7_pin15),
    .pin16(1'b1));
  _7485 x_scan_cmp4_bits_4_7 (
    .pin1(x_scan_cmp4_bits_0_3_pin9[7]), .pin2(x_scan_cmp4_bits_0_3_pin7), .pin3(x_scan_cmp4_bits_0_3_pin6),
    .pin4(x_scan_cmp4_bits_0_3_pin5), .pin5(x_scan_cmp4_bits_4_7_pin5), .pin6(x_scan_cmp4_bits_4_7_pin6),
    .pin7(x_scan_cmp4_bits_4_7_pin7), .pin8(1'b0), .pin9(x_scan_cmp4_bits_0_3_pin9[4]), .pin10(x_scan_b4),
    .pin11(x_scan_cmp4_bits_0_3_pin9[5]), .pin12(x_scan_b5), .pin13(x_scan_b6),
    .pin14(x_scan_cmp4_bits_0_3_pin9[6]), .pin15(x_scan_b7), .pin16(1'b1));
  _7485 x_scan_cmp6_bits_4_7 (
    .pin1(x_scan_cmp6_bits_0_3_pin9[7]), .pin2(x_scan_cmp6_bits_0_3_pin7), .pin3(x_scan_cmp6_bits_0_3_pin6),
    .pin4(x_scan_cmp6_bits_0_3_pin5), .pin5(x_scan_cmp6_bits_4_7_pin5), .pin6(x_scan_cmp6_bits_4_7_pin6),
    .pin7(x_scan_cmp6_bits_4_7_pin7), .pin8(1'b0), .pin9(x_scan_cmp6_bits_0_3_pin9[4]), .pin10(x_scan_b4),
    .pin11(x_scan_cmp6_bits_0_3_pin9[5]), .pin12(x_scan_b5), .pin13(x_scan_b6),
    .pin14(x_scan_cmp6_bits_0_3_pin9[6]), .pin15(x_scan_b7), .pin16(1'b1));
  _7485 x_scan_cmp8_bits_4_7 (
    .pin1(x_scan_cmp8_bits_0_3_pin9[7]), .pin2(x_scan_cmp8_bits_0_3_pin7), .pin3(x_scan_cmp8_bits_0_3_pin6),
    .pin4(x_scan_cmp8_bits_0_3_pin5), .pin5(x_scan_cmp8_bits_4_7_pin5), .pin6(x_scan_cmp8_bits_4_7_pin6),
    .pin7(x_scan_cmp8_bits_4_7_pin7), .pin8(1'b0), .pin9(x_scan_cmp8_bits_0_3_pin9[4]), .pin10(x_scan_b4),
    .pin11(x_scan_cmp8_bits_0_3_pin9[5]), .pin12(x_scan_b5), .pin13(x_scan_b6),
    .pin14(x_scan_cmp8_bits_0_3_pin9[6]), .pin15(x_scan_b7), .pin16(1'b1));
  _7485 y_scan_cmp4_bits_4_7 (
    .pin1(y_scan_cmp4_bits_0_3_pin9[7]), .pin2(y_scan_cmp4_bits_0_3_pin7), .pin3(y_scan_cmp4_bits_0_3_pin6),
    .pin4(y_scan_cmp4_bits_0_3_pin5), .pin5(y_scan_cmp4_bits_4_7_pin5), .pin6(y_scan_cmp4_bits_4_7_pin6),
    .pin7(y_scan_cmp4_bits_4_7_pin7), .pin8(1'b0), .pin9(y_scan_cmp4_bits_0_3_pin9[4]), .pin10(y_scan_b4),
    .pin11(y_scan_cmp4_bits_0_3_pin9[5]), .pin12(y_scan_b5), .pin13(y_scan_b6),
    .pin14(y_scan_cmp4_bits_0_3_pin9[6]), .pin15(y_scan_b7), .pin16(1'b1));
  _7485 y_scan_cmp6_bits_4_7 (
    .pin1(y_scan_cmp6_bits_0_3_pin9[7]), .pin2(y_scan_cmp6_bits_0_3_pin7), .pin3(y_scan_cmp6_bits_0_3_pin6),
    .pin4(y_scan_cmp6_bits_0_3_pin5), .pin5(y_scan_cmp6_bits_4_7_pin5), .pin6(y_scan_cmp6_bits_4_7_pin6),
    .pin7(y_scan_cmp6_bits_4_7_pin7), .pin8(1'b0), .pin9(y_scan_cmp6_bits_0_3_pin9[4]), .pin10(y_scan_b4),
    .pin11(y_scan_cmp6_bits_0_3_pin9[5]), .pin12(y_scan_b5), .pin13(y_scan_b6),
    .pin14(y_scan_cmp6_bits_0_3_pin9[6]), .pin15(y_scan_b7), .pin16(1'b1));
  _7485 y_scan_cmp8_bits_4_7 (
    .pin1(y_scan_cmp8_bits_0_3_pin9[7]), .pin2(y_scan_cmp8_bits_0_3_pin7), .pin3(y_scan_cmp8_bits_0_3_pin6),
    .pin4(y_scan_cmp8_bits_0_3_pin5), .pin5(y_scan_cmp8_bits_4_7_pin5), .pin6(y_scan_cmp8_bits_4_7_pin6),
    .pin7(y_scan_cmp8_bits_4_7_pin7), .pin8(1'b0), .pin9(y_scan_cmp8_bits_0_3_pin9[4]), .pin10(y_scan_b4),
    .pin11(y_scan_cmp8_bits_0_3_pin9[5]), .pin12(y_scan_b5), .pin13(y_scan_b6),
    .pin14(y_scan_cmp8_bits_0_3_pin9[6]), .pin15(y_scan_b7), .pin16(1'b1));
  _74163 x_scan_counter_bits_8_11 (
    .pin1(x_scan_clear_n), .pin2(pixel_clock), .pin3(1'b0), .pin4(1'b0), .pin5(1'b0), .pin6(1'b0),
    .pin7(1'b1), .pin8(1'b0), .pin9(1'b1), .pin10(x_scan_counter_bits_4_7_pin15), .pin11(XSCAN_B11),
    .pin12(XSCAN_B10), .pin13(x_scan_b9), .pin14(x_scan_b8), .pin16(1'b1));  // open: pin15
  _74163 y_scan_counter_bits_8_11 (
    .pin1(y_scan_clear_n), .pin2(x_scan_clear_n), .pin3(1'b0), .pin4(1'b0), .pin5(1'b0), .pin6(1'b0),
    .pin7(1'b1), .pin8(1'b0), .pin9(1'b1), .pin10(y_scan_counter_bits_4_7_pin15),
    .pin11(y_scan_counter_bits_8_11_pin11), .pin12(y_scan_counter_bits_8_11_pin12), .pin13(y_scan_b9),
    .pin14(y_scan_b8), .pin16(1'b1));  // open: pin15
  _7485 x_scan_cmp4_bits_8_11 (
    .pin1(x_scan_cmp4_bits_0_3_pin9[11]), .pin2(x_scan_cmp4_bits_4_7_pin7), .pin3(x_scan_cmp4_bits_4_7_pin6),
    .pin4(x_scan_cmp4_bits_4_7_pin5), .pin5(x_scan_gt_4), .pin6(x_scan_eq_4), .pin7(x_scan_lt_4),
    .pin8(1'b0), .pin9(x_scan_cmp4_bits_0_3_pin9[8]), .pin10(x_scan_b8),
    .pin11(x_scan_cmp4_bits_0_3_pin9[9]), .pin12(x_scan_b9), .pin13(XSCAN_B10),
    .pin14(x_scan_cmp4_bits_0_3_pin9[10]), .pin15(XSCAN_B11), .pin16(1'b1));
  _7485 x_scan_cmp6_bits_8_11 (
    .pin1(x_scan_cmp6_bits_0_3_pin9[11]), .pin2(x_scan_cmp6_bits_4_7_pin7), .pin3(x_scan_cmp6_bits_4_7_pin6),
    .pin4(x_scan_cmp6_bits_4_7_pin5), .pin5(x_scan_gt_6), .pin6(x_scan_eq_6), .pin7(x_scan_lt_6),
    .pin8(1'b0), .pin9(x_scan_cmp6_bits_0_3_pin9[8]), .pin10(x_scan_b8),
    .pin11(x_scan_cmp6_bits_0_3_pin9[9]), .pin12(x_scan_b9), .pin13(XSCAN_B10),
    .pin14(x_scan_cmp6_bits_0_3_pin9[10]), .pin15(XSCAN_B11), .pin16(1'b1));
  _7485 x_scan_cmp8_bits_8_11 (
    .pin1(x_scan_cmp8_bits_0_3_pin9[11]), .pin2(x_scan_cmp8_bits_4_7_pin7), .pin3(x_scan_cmp8_bits_4_7_pin6),
    .pin4(x_scan_cmp8_bits_4_7_pin5), .pin5(x_scan_gt_8), .pin6(x_scan_eq_8), .pin7(x_scan_clear_n),
    .pin8(1'b0), .pin9(x_scan_cmp8_bits_0_3_pin9[8]), .pin10(x_scan_b8),
    .pin11(x_scan_cmp8_bits_0_3_pin9[9]), .pin12(x_scan_b9), .pin13(XSCAN_B10),
    .pin14(x_scan_cmp8_bits_0_3_pin9[10]), .pin15(XSCAN_B11), .pin16(1'b1));
  _7485 y_scan_cmp4_bits_8_11 (
    .pin1(y_scan_cmp4_bits_0_3_pin9[11]), .pin2(y_scan_cmp4_bits_4_7_pin7), .pin3(y_scan_cmp4_bits_4_7_pin6),
    .pin4(y_scan_cmp4_bits_4_7_pin5), .pin5(y_scan_gt_4), .pin6(y_scan_eq_4), .pin7(y_scan_lt_4),
    .pin8(1'b0), .pin9(y_scan_cmp4_bits_0_3_pin9[8]), .pin10(y_scan_b8),
    .pin11(y_scan_cmp4_bits_0_3_pin9[9]), .pin12(y_scan_b9), .pin13(y_scan_counter_bits_8_11_pin12),
    .pin14(y_scan_cmp4_bits_0_3_pin9[10]), .pin15(y_scan_counter_bits_8_11_pin11), .pin16(1'b1));
  _7485 y_scan_cmp6_bits_8_11 (
    .pin1(y_scan_cmp6_bits_0_3_pin9[11]), .pin2(y_scan_cmp6_bits_4_7_pin7), .pin3(y_scan_cmp6_bits_4_7_pin6),
    .pin4(y_scan_cmp6_bits_4_7_pin5), .pin5(y_scan_gt_6), .pin6(y_scan_eq_6), .pin7(y_scan_lt_6),
    .pin8(1'b0), .pin9(y_scan_cmp6_bits_0_3_pin9[8]), .pin10(y_scan_b8),
    .pin11(y_scan_cmp6_bits_0_3_pin9[9]), .pin12(y_scan_b9), .pin13(y_scan_counter_bits_8_11_pin12),
    .pin14(y_scan_cmp6_bits_0_3_pin9[10]), .pin15(y_scan_counter_bits_8_11_pin11), .pin16(1'b1));
  _7485 y_scan_cmp8_bits_8_11 (
    .pin1(y_scan_cmp8_bits_0_3_pin9[11]), .pin2(y_scan_cmp8_bits_4_7_pin7), .pin3(y_scan_cmp8_bits_4_7_pin6),
    .pin4(y_scan_cmp8_bits_4_7_pin5), .pin5(y_scan_gt_8), .pin6(y_scan_eq_8), .pin7(y_scan_clear_n),
    .pin8(1'b0), .pin9(y_scan_cmp8_bits_0_3_pin9[8]), .pin10(y_scan_b8),
    .pin11(y_scan_cmp8_bits_0_3_pin9[9]), .pin12(y_scan_b9), .pin13(y_scan_counter_bits_8_11_pin12),
    .pin14(y_scan_cmp8_bits_0_3_pin9[10]), .pin15(y_scan_counter_bits_8_11_pin11), .pin16(1'b1));
  nand x_test_window_nand (hsync_n, x_scan_gt_4, x_scan_lt_6);
  nand y_test_window_nand (vsync_n, y_scan_gt_4, y_scan_lt_6);
  _74283 x_paddle_plus40_bits_0_3 (
    .pin1(x_paddle_right_b1), .pin2(PWIDTH40_B1), .pin3(1'b0), .pin4(x_paddle_right_b0), .pin5(1'b0),
    .pin6(PWIDTH40_B0), .pin7(1'b0), .pin8(1'b0), .pin9(XP40_PLUS40_CARRY_0), .pin10(x_paddle_right_b3),
    .pin11(PWIDTH40_B3), .pin12(paddle_d3), .pin13(x_paddle_right_b2), .pin14(1'b0), .pin15(PWIDTH40_B2),
    .pin16(1'b1));
  _7485 cmp_xscan_vs_paddle_left_bits_0_3 (
    .pin1(paddle_d3), .pin2(cmp_xscan_vs_paddle_left_bits_0_3_pin2[0]),
    .pin3(cmp_xscan_vs_paddle_left_bits_0_3_pin2[1]), .pin4(cmp_xscan_vs_paddle_left_bits_0_3_pin2[2]),
    .pin5(cmp_xscan_vs_paddle_left_CASCADE_0_GT), .pin6(cmp_xscan_vs_paddle_left_CASCADE_0_EQ),
    .pin7(cmp_xscan_vs_paddle_left_CASCADE_0_LT), .pin8(1'b0), .pin9(1'b0), .pin10(x_scan_b0), .pin11(1'b0),
    .pin12(x_scan_b1), .pin13(x_scan_b2), .pin14(1'b0), .pin15(x_scan_b3), .pin16(1'b1));
  _7485 cmp_xscan_vs_paddle_right_bits_0_3 (
    .pin1(x_paddle_right_b3), .pin2(cmp_xscan_vs_paddle_right_bits_0_3_pin2[0]),
    .pin3(cmp_xscan_vs_paddle_right_bits_0_3_pin2[1]), .pin4(cmp_xscan_vs_paddle_right_bits_0_3_pin2[2]),
    .pin5(cmp_xscan_vs_paddle_right_CASCADE_0_GT), .pin6(cmp_xscan_vs_paddle_right_CASCADE_0_EQ),
    .pin7(cmp_xscan_vs_paddle_right_CASCADE_0_LT), .pin8(1'b0), .pin9(x_paddle_right_b0), .pin10(x_scan_b0),
    .pin11(x_paddle_right_b1), .pin12(x_scan_b1), .pin13(x_scan_b2), .pin14(x_paddle_right_b2),
    .pin15(x_scan_b3), .pin16(1'b1));
  _74283 x_paddle_plus40_bits_4_7 (
    .pin1(x_paddle_right_b5), .pin2(PWIDTH40_B5), .pin3(x_paddle_px_b5), .pin4(x_paddle_right_b4),
    .pin5(paddle_d2), .pin6(PWIDTH40_B4), .pin7(XP40_PLUS40_CARRY_0), .pin8(1'b0),
    .pin9(XP40_PLUS40_CARRY_1), .pin10(x_paddle_right_b7), .pin11(PWIDTH40_B7), .pin12(x_paddle_px_b7),
    .pin13(x_paddle_right_b6), .pin14(x_paddle_px_b6), .pin15(PWIDTH40_B6), .pin16(1'b1));
  _7485 cmp_xscan_vs_paddle_left_bits_4_7 (
    .pin1(x_paddle_px_b7), .pin2(cmp_xscan_vs_paddle_left_CASCADE_0_LT),
    .pin3(cmp_xscan_vs_paddle_left_CASCADE_0_EQ), .pin4(cmp_xscan_vs_paddle_left_CASCADE_0_GT),
    .pin5(cmp_xscan_vs_paddle_left_CASCADE_1_GT), .pin6(cmp_xscan_vs_paddle_left_CASCADE_1_EQ),
    .pin7(cmp_xscan_vs_paddle_left_CASCADE_1_LT), .pin8(1'b0), .pin9(paddle_d2), .pin10(x_scan_b4),
    .pin11(x_paddle_px_b5), .pin12(x_scan_b5), .pin13(x_scan_b6), .pin14(x_paddle_px_b6), .pin15(x_scan_b7),
    .pin16(1'b1));
  _7485 cmp_xscan_vs_paddle_right_bits_4_7 (
    .pin1(x_paddle_right_b7), .pin2(cmp_xscan_vs_paddle_right_CASCADE_0_LT),
    .pin3(cmp_xscan_vs_paddle_right_CASCADE_0_EQ), .pin4(cmp_xscan_vs_paddle_right_CASCADE_0_GT),
    .pin5(cmp_xscan_vs_paddle_right_CASCADE_1_GT), .pin6(cmp_xscan_vs_paddle_right_CASCADE_1_EQ),
    .pin7(cmp_xscan_vs_paddle_right_CASCADE_1_LT), .pin8(1'b0), .pin9(x_paddle_right_b4), .pin10(x_scan_b4),
    .pin11(x_paddle_right_b5), .pin12(x_scan_b5), .pin13(x_scan_b6), .pin14(x_paddle_right_b6),
    .pin15(x_scan_b7), .pin16(1'b1));
  _74283 x_paddle_plus40_bits_8_11 (
    .pin1(x_paddle_right_b9), .pin2(PWIDTH40_B9), .pin3(x_paddle_px_b9), .pin4(x_paddle_right_b8),
    .pin5(x_paddle_px_b8), .pin6(PWIDTH40_B8), .pin7(XP40_PLUS40_CARRY_1), .pin8(1'b0),
    .pin10(XP40_RIGHT_B11), .pin11(PWIDTH40_B11), .pin12(1'b0), .pin13(XP40_RIGHT_B10), .pin14(1'b0),
    .pin15(PWIDTH40_B10), .pin16(1'b1));  // open: pin9
  _7485 cmp_xscan_vs_paddle_left_bits_8_11 (
    .pin1(1'b0), .pin2(cmp_xscan_vs_paddle_left_CASCADE_1_LT), .pin3(cmp_xscan_vs_paddle_left_CASCADE_1_EQ),
    .pin4(cmp_xscan_vs_paddle_left_CASCADE_1_GT), .pin5(x_scan_gt_paddle_left),
    .pin6(cmp_xscan_vs_paddle_left_EQ), .pin7(cmp_xscan_vs_paddle_left_LT), .pin8(1'b0),
    .pin9(x_paddle_px_b8), .pin10(x_scan_b8), .pin11(x_paddle_px_b9), .pin12(x_scan_b9), .pin13(XSCAN_B10),
    .pin14(1'b0), .pin15(XSCAN_B11), .pin16(1'b1));
  _7485 cmp_xscan_vs_paddle_right_bits_8_11 (
    .pin1(XP40_RIGHT_B11), .pin2(cmp_xscan_vs_paddle_right_CASCADE_1_LT),
    .pin3(cmp_xscan_vs_paddle_right_CASCADE_1_EQ), .pin4(cmp_xscan_vs_paddle_right_CASCADE_1_GT),
    .pin5(cmp_xscan_vs_paddle_right_GT), .pin6(cmp_xscan_vs_paddle_right_EQ), .pin7(x_scan_lt_paddle_right),
    .pin8(1'b0), .pin9(x_paddle_right_b8), .pin10(x_scan_b8), .pin11(x_paddle_right_b9), .pin12(x_scan_b9),
    .pin13(XSCAN_B10), .pin14(XP40_RIGHT_B10), .pin15(XSCAN_B11), .pin16(1'b1));
  // And paddle_x_window_and has open pins: In_1=x_scan_gt_paddle_left, In_2=x_scan_lt_paddle_right, out=open

  assign x_paddle_px_b0 = 1'b0;
  assign x_paddle_px_b1 = 1'b0;
  assign x_paddle_px_b2 = 1'b0;
  assign x_paddle_px_b3 = paddle_d3;
  assign x_paddle_px_b4 = paddle_d2;
  assign x_scan_lt_8 = x_scan_clear_n;
  assign y_scan_lt_8 = y_scan_clear_n;
  // also tied to GND on the sheet: {x_scan_cmp4_bits_0_3_pin9[0], x_scan_cmp4_bits_0_3_pin9[1], x_scan_cmp4_bits_0_3_pin9[3], x_scan_cmp4_bits_0_3_pin9[4], x_scan_cmp4_bits_0_3_pin9[5], x_scan_cmp4_bits_0_3_pin9[6], x_scan_cmp4_bits_0_3_pin9[7], x_scan_cmp4_bits_0_3_pin9[8], x_scan_cmp4_bits_0_3_pin9[9], x_scan_cmp4_bits_0_3_pin9[10], x_scan_cmp4_bits_0_3_pin9[11], x_scan_cmp6_bits_0_3_pin9[0], x_scan_cmp6_bits_0_3_pin9[3], x_scan_cmp6_bits_0_3_pin9[4], x_scan_cmp6_bits_0_3_pin9[5], x_scan_cmp6_bits_0_3_pin9[6], x_scan_cmp6_bits_0_3_pin9[7], x_scan_cmp6_bits_0_3_pin9[8], x_scan_cmp6_bits_0_3_pin9[9], x_scan_cmp6_bits_0_3_pin9[10], x_scan_cmp6_bits_0_3_pin9[11], x_scan_cmp8_bits_0_3_pin9[0], x_scan_cmp8_bits_0_3_pin9[1], x_scan_cmp8_bits_0_3_pin9[2], x_scan_cmp8_bits_0_3_pin9[4], x_scan_cmp8_bits_0_3_pin9[5], x_scan_cmp8_bits_0_3_pin9[6], x_scan_cmp8_bits_0_3_pin9[7], x_scan_cmp8_bits_0_3_pin9[8], x_scan_cmp8_bits_0_3_pin9[9], x_scan_cmp8_bits_0_3_pin9[10], x_scan_cmp8_bits_0_3_pin9[11], y_scan_cmp4_bits_0_3_pin9[0], y_scan_cmp4_bits_0_3_pin9[1], y_scan_cmp4_bits_0_3_pin9[3], y_scan_cmp4_bits_0_3_pin9[4], y_scan_cmp4_bits_0_3_pin9[5], y_scan_cmp4_bits_0_3_pin9[6], y_scan_cmp4_bits_0_3_pin9[7], y_scan_cmp4_bits_0_3_pin9[8], y_scan_cmp4_bits_0_3_pin9[9], y_scan_cmp4_bits_0_3_pin9[10], y_scan_cmp4_bits_0_3_pin9[11], y_scan_cmp6_bits_0_3_pin9[0], y_scan_cmp6_bits_0_3_pin9[3], y_scan_cmp6_bits_0_3_pin9[4], y_scan_cmp6_bits_0_3_pin9[5], y_scan_cmp6_bits_0_3_pin9[6], y_scan_cmp6_bits_0_3_pin9[7], y_scan_cmp6_bits_0_3_pin9[8], y_scan_cmp6_bits_0_3_pin9[9], y_scan_cmp6_bits_0_3_pin9[10], y_scan_cmp6_bits_0_3_pin9[11], y_scan_cmp8_bits_0_3_pin9[0], y_scan_cmp8_bits_0_3_pin9[1], y_scan_cmp8_bits_0_3_pin9[2], y_scan_cmp8_bits_0_3_pin9[4], y_scan_cmp8_bits_0_3_pin9[5], y_scan_cmp8_bits_0_3_pin9[6], y_scan_cmp8_bits_0_3_pin9[7], y_scan_cmp8_bits_0_3_pin9[8], y_scan_cmp8_bits_0_3_pin9[9], y_scan_cmp8_bits_0_3_pin9[10], y_scan_cmp8_bits_0_3_pin9[11], x_scan_cmp4_bits_0_3_pin2[0], x_scan_cmp4_bits_0_3_pin2[2], x_scan_cmp6_bits_0_3_pin2[0], x_scan_cmp6_bits_0_3_pin2[2], x_scan_cmp8_bits_0_3_pin2[0], x_scan_cmp8_bits_0_3_pin2[2], y_scan_cmp4_bits_0_3_pin2[0], y_scan_cmp4_bits_0_3_pin2[2], y_scan_cmp6_bits_0_3_pin2[0], y_scan_cmp6_bits_0_3_pin2[2], y_scan_cmp8_bits_0_3_pin2[0], y_scan_cmp8_bits_0_3_pin2[2], PWIDTH40_B0, PWIDTH40_B1, PWIDTH40_B2, PWIDTH40_B4, PWIDTH40_B6, PWIDTH40_B7, PWIDTH40_B8, PWIDTH40_B9, PWIDTH40_B10, PWIDTH40_B11, cmp_xscan_vs_paddle_left_bits_0_3_pin2[0], cmp_xscan_vs_paddle_left_bits_0_3_pin2[2], cmp_xscan_vs_paddle_right_bits_0_3_pin2[0], cmp_xscan_vs_paddle_right_bits_0_3_pin2[2]}
  // also tied to VCC on the sheet: {x_scan_cmp4_bits_0_3_pin9[2], x_scan_cmp6_bits_0_3_pin9[1], x_scan_cmp6_bits_0_3_pin9[2], x_scan_cmp8_bits_0_3_pin9[3], y_scan_cmp4_bits_0_3_pin9[2], y_scan_cmp6_bits_0_3_pin9[1], y_scan_cmp6_bits_0_3_pin9[2], y_scan_cmp8_bits_0_3_pin9[3], x_scan_cmp4_bits_0_3_pin2[1], x_scan_cmp6_bits_0_3_pin2[1], x_scan_cmp8_bits_0_3_pin2[1], y_scan_cmp4_bits_0_3_pin2[1], y_scan_cmp6_bits_0_3_pin2[1], y_scan_cmp8_bits_0_3_pin2[1], PWIDTH40_B3, PWIDTH40_B5, cmp_xscan_vs_paddle_left_bits_0_3_pin2[1], cmp_xscan_vs_paddle_right_bits_0_3_pin2[1]}

  // Other names for the same wires on the sheet: cmp_xscan_vs_paddle_left_GT = x_scan_gt_paddle_left;
  //   cmp_xscan_vs_paddle_right_LT = x_scan_lt_paddle_right; PADDLE_Q0 = paddle_d3; PADDLE_Q1 = paddle_d2;
  //   PADDLE_Q2 = paddle_d1; PADDLE_Q3 = paddle_d0; XP40_B5 = x_paddle_px_b5; XP40_B6 = x_paddle_px_b6;
  //   XP40_B7 = x_paddle_px_b7; XP40_B8 = x_paddle_px_b8; XP40_B9 = x_paddle_px_b9; XP40_RIGHT_B0 = x_paddle_right_b0;
  //   XP40_RIGHT_B1 = x_paddle_right_b1; XP40_RIGHT_B2 = x_paddle_right_b2; XP40_RIGHT_B3 = x_paddle_right_b3;
  //   XP40_RIGHT_B4 = x_paddle_right_b4; XP40_RIGHT_B5 = x_paddle_right_b5; XP40_RIGHT_B6 = x_paddle_right_b6;
  //   XP40_RIGHT_B7 = x_paddle_right_b7; XP40_RIGHT_B8 = x_paddle_right_b8; XP40_RIGHT_B9 = x_paddle_right_b9;
  //   XSCAN_B0 = x_scan_b0; XSCAN_B1 = x_scan_b1; XSCAN_B2 = x_scan_b2; XSCAN_B3 = x_scan_b3; XSCAN_B4 = x_scan_b4;
  //   XSCAN_B5 = x_scan_b5; XSCAN_B6 = x_scan_b6; XSCAN_B7 = x_scan_b7; XSCAN_B8 = x_scan_b8; XSCAN_B9 = x_scan_b9

  // Notes on the sheet:
  //   X_Paddle
  //   PADDLE X × 40
  //   40·X = (X << 5) + (X << 3)
  //   uscita: 0, 40, 80, …, 600
  //   x_paddle_px[9:0]
  //   TEST_START = 4
  //   10 bit: 0000000100
  //   4 stored as a 12-bit constant: 0000 0000 0100
  //   TEST_END = 6
  //   10 bit: 0000000110
  //   6 stored as a 12-bit constant: 0000 0000 0110
  //   TEST_LINE_END = 8
  //   12 bit: 0000 0000 1000
  //   Y clock: fronte di salita di x_scan_lt_8 (una volta per riga di prova)
  //   TEST_FRAME_END = 8
  //   X_SCAN COUNTER (10 bit usati)
  //   Y_SCAN COUNTER (10 bit usati)
  //   X_SCAN vs TEST_START
  //   X_SCAN vs TEST_END
  //   X_SCAN vs TEST_LINE_END
  //   Y_SCAN vs TEST_START
  //   Y_SCAN vs TEST_END
  //   Y_SCAN vs TEST_FRAME_END
  //   PADDLE RIGHT EDGE = X_paddle_px + 40
  //   12-bit addition; range 40 ... 640
  //   X_SCAN > X_PADDLE_LEFT
  //   X_SCAN < X_PADDLE_RIGHT (= LEFT + 40)
  //   PADDLE HORIZONTAL WINDOW
endmodule
