// Digital circuit circuit_test_final_no_tunnels_or_times100_CORRETTO.dig as structural Verilog
module circuit_test_final_no_tunnels_or_times100_CORRETTO (
  input  paddle_down,
  input  paddle_up,
  input  paddle_load_n,
  input  paddle_clear,
  input  paddle_q2_in,
  input  paddle_q3_in,
  input  paddle_q1_in,
  input  paddle_q0_in,
  input  pixel_clock,
  output paddle_d0,
  output paddle_d1,
  output paddle_d2,
  output paddle_d3,
  output paddle_borrow_out,
  output paddle_carry_out,
  output x_scan_b0,
  output x_scan_b1,
  output x_scan_b2,
  output x_scan_b3,
  output x_scan_b4,
  output x_scan_b5,
  output x_scan_b6,
  output x_scan_b7,
  output x_scan_b8,
  output x_scan_b9,
  output x_scan_gt_4,
  output x_scan_eq_4,
  output x_scan_lt_4,
  output x_scan_gt_6,
  output x_scan_eq_6,
  output x_scan_lt_6,
  output hsync_n,
  output x_scan_gt_8,
  output x_scan_eq_8,
  output x_scan_lt_8,
  output x_scan_clear_n,
  output y_scan_b0,
  output y_scan_b1,
  output y_scan_b2,
  output y_scan_b3,
  output y_scan_b4,
  output y_scan_b5,
  output y_scan_b6,
  output y_scan_b7,
  output y_scan_b8,
  output y_scan_b9,
  output y_scan_gt_4,
  output y_scan_eq_4,
  output y_scan_lt_4,
  output y_scan_gt_6,
  output y_scan_eq_6,
  output y_scan_lt_6,
  output vsync_n,
  output y_scan_gt_8,
  output y_scan_eq_8,
  output y_scan_lt_8,
  output y_scan_clear_n,
  output x_paddle_px_b0,
  output x_paddle_px_b1,
  output x_paddle_px_b2,
  output x_paddle_px_b3,
  output x_paddle_px_b4,
  output x_paddle_px_b5,
  output x_paddle_px_b6,
  output x_paddle_px_b7,
  output x_paddle_px_b8,
  output x_paddle_px_b9,
  output x_scan_gt_paddle_x40,
  output x_scan_lt_paddle_x40_plus40,
  output y_scan_gt_460,
  output y_scan_lt_475,
  output paddle_x_visible,
  output paddle_y_visible,
  output paddle_visible,
  output final_or_out,
  output final_or_times100_b0,
  output final_or_times100_b1,
  output final_or_times100_b2,
  output final_or_times100_b3,
  output final_or_times100_b4,
  output final_or_times100_b5,
  output final_or_times100_b6
);

  wire cmp1_xscan_gt_pad40_bits_0_3_pin5, cmp1_xscan_gt_pad40_bits_0_3_pin6,
       cmp1_xscan_gt_pad40_bits_0_3_pin7, cmp1_xscan_gt_pad40_bits_4_7_pin5,
       cmp1_xscan_gt_pad40_bits_4_7_pin6, cmp1_xscan_gt_pad40_bits_4_7_pin7,
       cmp2_paddle_plus40_bits_0_3_pin1, cmp2_paddle_plus40_bits_0_3_pin4, cmp2_paddle_plus40_bits_4_7_pin1,
       cmp2_paddle_plus40_bits_4_7_pin4, cmp2_paddle_plus40_bits_8_11_pin1,
       cmp2_paddle_plus40_bits_8_11_pin4, cmp2_xscan_lt_padright_bits_0_3_pin5,
       cmp2_xscan_lt_padright_bits_0_3_pin6, cmp2_xscan_lt_padright_bits_0_3_pin7,
       cmp2_xscan_lt_padright_bits_4_7_pin5, cmp2_xscan_lt_padright_bits_4_7_pin6,
       cmp2_xscan_lt_padright_bits_4_7_pin7, PADDLE_XY_FINAL_AND_out, x_scan_cmp4_bits_0_3_pin2,
       x_scan_cmp4_bits_0_3_pin4, x_scan_cmp6_bits_0_3_pin2, x_scan_cmp6_bits_0_3_pin4,
       x_scan_cmp8_bits_0_3_pin2, x_scan_cmp8_bits_0_3_pin4, y_scan_cmp4_bits_0_3_pin2,
       y_scan_cmp4_bits_0_3_pin4, y_scan_cmp6_bits_0_3_pin2, y_scan_cmp6_bits_0_3_pin4,
       y_scan_cmp8_bits_0_3_pin2, y_scan_cmp8_bits_0_3_pin4, ycmp1_gt460_bits_0_3_pin5,
       ycmp1_gt460_bits_0_3_pin6, ycmp1_gt460_bits_0_3_pin7, ycmp1_gt460_bits_4_7_pin5,
       ycmp1_gt460_bits_4_7_pin6, ycmp1_gt460_bits_4_7_pin7, ycmp2_lt475_bits_0_3_pin5,
       ycmp2_lt475_bits_0_3_pin6, ycmp2_lt475_bits_0_3_pin7, ycmp2_lt475_bits_4_7_pin5,
       ycmp2_lt475_bits_4_7_pin6, ycmp2_lt475_bits_4_7_pin7;
  wire [2:0] cmp1_xscan_gt_pad40_bits_0_3_pin2, cmp2_xscan_lt_padright_bits_0_3_pin2,
       ycmp1_gt460_bits_0_3_pin2, ycmp2_lt475_bits_0_3_pin2;
  wire [10:0] cmp2_paddle_plus40_bits_0_3_pin6;
  wire [11:0] ycmp1_gt460_bits_0_3_pin9, ycmp2_lt475_bits_0_3_pin9;

  _74193 x_paddle_counter (
    .pin1(paddle_load_n), .pin2(paddle_down), .pin3(paddle_down), .pin4(paddle_down), .pin5(paddle_down),
    .pin6(paddle_down), .pin7(paddle_down), .pin8(paddle_down), .pin9(paddle_q3_in), .pin10(paddle_q2_in),
    .pin11(paddle_q1_in), .pin12(paddle_borrow_out), .pin13(paddle_carry_out), .pin14(paddle_q0_in),
    .pin15(paddle_clear), .pin16(1'b1));
  _74283 x_paddle_times_40_adder (
    .pin1(paddle_down), .pin4(paddle_down), .pin6(paddle_down), .pin7(1'b0), .pin8(1'b0),
    .pin9(x_paddle_px_b9), .pin10(x_paddle_px_b8), .pin11(1'b0), .pin12(paddle_down), .pin13(paddle_down),
    .pin14(paddle_down), .pin15(1'b0), .pin16(1'b1));  // open: pin2, pin3, pin5
  _74163 x_scan_counter_bits_0_3 (
    .pin1(1'b1), .pin3(1'b0), .pin4(1'b0), .pin5(1'b0), .pin6(1'b0), .pin7(1'b1), .pin8(1'b0), .pin9(1'b1),
    .pin10(1'b1), .pin11(paddle_down), .pin12(paddle_down), .pin13(paddle_down), .pin14(paddle_down),
    .pin16(1'b1));  // open: pin2, pin15
  _74163 y_scan_counter_bits_0_3 (
    .pin1(y_scan_lt_8), .pin3(1'b0), .pin4(1'b0), .pin5(1'b0), .pin6(1'b0), .pin7(1'b1), .pin8(1'b0),
    .pin9(1'b1), .pin10(1'b1), .pin11(1'b0), .pin12(1'b0), .pin13(1'b0), .pin14(1'b0), .pin16(1'b1));  // open: pin2, pin15
  _7485 x_scan_cmp4_bits_0_3 (
    .pin2(x_scan_cmp4_bits_0_3_pin2), .pin4(x_scan_cmp4_bits_0_3_pin4), .pin5(paddle_down),
    .pin8(paddle_down), .pin10(paddle_down), .pin12(paddle_down), .pin13(paddle_down), .pin15(paddle_down));  // open: pin1, pin3, pin6, pin7, pin9, pin11, pin14, pin16
  _7485 x_scan_cmp6_bits_0_3 (
    .pin2(x_scan_cmp6_bits_0_3_pin2), .pin4(x_scan_cmp6_bits_0_3_pin4), .pin5(paddle_down),
    .pin8(paddle_down), .pin10(paddle_down), .pin12(paddle_down), .pin13(paddle_down), .pin15(paddle_down));  // open: pin1, pin3, pin6, pin7, pin9, pin11, pin14, pin16
  _7485 x_scan_cmp8_bits_0_3 (
    .pin2(x_scan_cmp8_bits_0_3_pin2), .pin4(x_scan_cmp8_bits_0_3_pin4), .pin5(paddle_down),
    .pin7(paddle_down), .pin8(paddle_down), .pin10(paddle_down), .pin12(paddle_down), .pin13(paddle_down),
    .pin15(paddle_down));  // open: pin1, pin3, pin6, pin9, pin11, pin14, pin16
  _7485 y_scan_cmp4_bits_0_3 (
    .pin2(y_scan_cmp4_bits_0_3_pin2), .pin4(y_scan_cmp4_bits_0_3_pin4), .pin5(1'b0), .pin8(1'b0),
    .pin10(1'b0), .pin12(1'b0), .pin13(1'b0), .pin15(1'b0));  // open: pin1, pin3, pin6, pin7, pin9, pin11, pin14, pin16
  _7485 y_scan_cmp6_bits_0_3 (
    .pin2(y_scan_cmp6_bits_0_3_pin2), .pin4(y_scan_cmp6_bits_0_3_pin4), .pin5(1'b0), .pin8(1'b0),
    .pin10(1'b0), .pin12(1'b0), .pin13(1'b0), .pin15(1'b0));  // open: pin1, pin3, pin6, pin7, pin9, pin11, pin14, pin16
  _7485 y_scan_cmp8_bits_0_3 (
    .pin2(y_scan_cmp8_bits_0_3_pin2), .pin4(y_scan_cmp8_bits_0_3_pin4), .pin5(1'b0), .pin7(1'b0),
    .pin8(1'b0), .pin10(1'b0), .pin12(1'b0), .pin13(1'b0), .pin15(1'b0));  // open: pin1, pin3, pin6, pin9, pin11, pin14, pin16
  _74163 x_scan_counter_bits_4_7 (
    .pin1(1'b1), .pin3(1'b0), .pin4(1'b0), .pin5(1'b0), .pin6(1'b0), .pin8(1'b0), .pin9(pixel_clock),
    .pin10(pixel_clock), .pin11(paddle_down), .pin12(paddle_down), .pin13(paddle_down), .pin14(paddle_down),
    .pin16(pixel_clock));  // open: pin2, pin7, pin15
  _74163 y_scan_counter_bits_4_7 (
    .pin1(y_scan_lt_8), .pin3(1'b0), .pin4(1'b0), .pin5(1'b0), .pin6(1'b0), .pin8(1'b0), .pin9(1'b1),
    .pin10(1'b1), .pin11(1'b0), .pin12(1'b0), .pin13(1'b0), .pin14(1'b0), .pin16(1'b1));  // open: pin2, pin7, pin15
  _7485 x_scan_cmp4_bits_4_7 (
    .pin2(paddle_down), .pin4(paddle_down), .pin5(paddle_down), .pin7(paddle_down), .pin8(paddle_down),
    .pin10(paddle_down), .pin12(paddle_down), .pin13(paddle_down), .pin15(paddle_down));  // open: pin1, pin3, pin6, pin9, pin11, pin14, pin16
  _7485 x_scan_cmp6_bits_4_7 (
    .pin2(paddle_down), .pin4(paddle_down), .pin5(paddle_down), .pin7(paddle_down), .pin8(paddle_down),
    .pin10(paddle_down), .pin12(paddle_down), .pin13(paddle_down), .pin15(paddle_down));  // open: pin1, pin3, pin6, pin9, pin11, pin14, pin16
  _7485 x_scan_cmp8_bits_4_7 (
    .pin2(paddle_down), .pin4(paddle_down), .pin5(paddle_down), .pin7(paddle_down), .pin8(paddle_down),
    .pin10(paddle_down), .pin12(paddle_down), .pin13(paddle_down), .pin15(paddle_down));  // open: pin1, pin3, pin6, pin9, pin11, pin14, pin16
  _7485 y_scan_cmp4_bits_4_7 (
    .pin2(1'b0), .pin4(1'b0), .pin5(1'b0), .pin7(1'b0), .pin8(1'b0), .pin10(1'b0), .pin12(1'b0),
    .pin13(1'b0), .pin15(1'b0));  // open: pin1, pin3, pin6, pin9, pin11, pin14, pin16
  _7485 y_scan_cmp6_bits_4_7 (
    .pin2(1'b0), .pin4(1'b0), .pin5(1'b0), .pin7(1'b0), .pin8(1'b0), .pin10(1'b0), .pin12(1'b0),
    .pin13(1'b0), .pin15(1'b0));  // open: pin1, pin3, pin6, pin9, pin11, pin14, pin16
  _7485 y_scan_cmp8_bits_4_7 (
    .pin2(1'b0), .pin4(1'b0), .pin5(1'b0), .pin7(1'b0), .pin8(1'b0), .pin10(1'b0), .pin12(1'b0),
    .pin13(1'b0), .pin15(1'b0));  // open: pin1, pin3, pin6, pin9, pin11, pin14, pin16
  _74163 x_scan_counter_bits_8_11 (
    .pin1(1'b1), .pin2(pixel_clock), .pin3(1'b0), .pin4(1'b0), .pin5(1'b0), .pin6(1'b0), .pin8(1'b0),
    .pin9(pixel_clock), .pin10(pixel_clock), .pin11(x_scan_b8), .pin12(x_scan_b8), .pin13(x_scan_b8),
    .pin14(x_scan_b8), .pin16(pixel_clock));  // open: pin7, pin15
  _74163 y_scan_counter_bits_8_11 (
    .pin1(y_scan_lt_8), .pin2(1'b1), .pin3(1'b0), .pin4(1'b0), .pin5(1'b0), .pin6(1'b0), .pin8(1'b0),
    .pin9(1'b1), .pin10(1'b1), .pin11(y_scan_b8), .pin12(y_scan_b8), .pin13(y_scan_b8), .pin14(y_scan_b8),
    .pin16(1'b1));  // open: pin7, pin15
  _7485 x_scan_cmp4_bits_8_11 (
    .pin1(1'b1), .pin2(paddle_down), .pin4(paddle_down), .pin5(x_scan_gt_4), .pin6(paddle_down),
    .pin7(x_scan_lt_4), .pin8(paddle_down), .pin9(paddle_down), .pin10(x_scan_b8), .pin11(paddle_down),
    .pin12(x_scan_b8), .pin13(x_scan_b8), .pin14(paddle_down), .pin15(x_scan_b8), .pin16(1'b1));  // open: pin3
  _7485 x_scan_cmp6_bits_8_11 (
    .pin1(1'b1), .pin2(paddle_down), .pin4(paddle_down), .pin5(x_scan_gt_6), .pin6(paddle_down),
    .pin7(x_scan_lt_6), .pin8(paddle_down), .pin9(paddle_down), .pin10(x_scan_b8), .pin11(paddle_down),
    .pin12(x_scan_b8), .pin13(x_scan_b8), .pin14(paddle_down), .pin15(x_scan_b8), .pin16(1'b1));  // open: pin3
  _7485 x_scan_cmp8_bits_8_11 (
    .pin1(1'b1), .pin2(paddle_down), .pin4(paddle_down), .pin5(x_scan_gt_8), .pin6(paddle_down), .pin7(1'b1),
    .pin8(paddle_down), .pin9(paddle_down), .pin10(x_scan_b8), .pin11(paddle_down), .pin12(x_scan_b8),
    .pin13(x_scan_b8), .pin14(paddle_down), .pin15(x_scan_b8), .pin16(1'b1));  // open: pin3
  _7485 y_scan_cmp4_bits_8_11 (
    .pin1(1'b1), .pin2(1'b0), .pin4(1'b0), .pin5(y_scan_gt_4), .pin6(1'b0), .pin7(y_scan_lt_4), .pin8(1'b0),
    .pin9(1'b0), .pin10(y_scan_b8), .pin11(1'b0), .pin12(y_scan_b8), .pin13(y_scan_b8), .pin14(1'b0),
    .pin15(y_scan_b8), .pin16(1'b1));  // open: pin3
  _7485 y_scan_cmp6_bits_8_11 (
    .pin1(1'b1), .pin2(1'b0), .pin4(1'b0), .pin5(y_scan_gt_6), .pin6(1'b0), .pin7(y_scan_lt_6), .pin8(1'b0),
    .pin9(1'b0), .pin10(y_scan_b8), .pin11(1'b0), .pin12(y_scan_b8), .pin13(y_scan_b8), .pin14(1'b0),
    .pin15(y_scan_b8), .pin16(1'b1));  // open: pin3
  _7485 y_scan_cmp8_bits_8_11 (
    .pin1(1'b1), .pin2(1'b0), .pin4(1'b0), .pin5(y_scan_gt_8), .pin6(1'b0), .pin7(y_scan_lt_8), .pin8(1'b0),
    .pin9(1'b0), .pin10(y_scan_b8), .pin11(1'b0), .pin12(y_scan_b8), .pin13(y_scan_b8), .pin14(1'b0),
    .pin15(y_scan_b8), .pin16(1'b1));  // open: pin3
  // NAnd x_test_window_nand is placed but not wired
  // NAnd y_test_window_nand is placed but not wired
  _7485 cmp1_xscan_gt_pad40_bits_0_3 (
    .pin1(paddle_down), .pin2(cmp1_xscan_gt_pad40_bits_0_3_pin2[0]),
    .pin3(cmp1_xscan_gt_pad40_bits_0_3_pin2[1]), .pin4(cmp1_xscan_gt_pad40_bits_0_3_pin2[2]),
    .pin5(cmp1_xscan_gt_pad40_bits_0_3_pin5), .pin6(cmp1_xscan_gt_pad40_bits_0_3_pin6),
    .pin7(cmp1_xscan_gt_pad40_bits_0_3_pin7), .pin8(1'b0), .pin9(1'b0), .pin10(paddle_down), .pin11(1'b0),
    .pin12(paddle_down), .pin13(paddle_down), .pin14(1'b0), .pin15(paddle_down), .pin16(1'b1));
  _74283 cmp2_paddle_plus40_bits_0_3 (
    .pin1(cmp2_paddle_plus40_bits_0_3_pin1), .pin2(cmp2_paddle_plus40_bits_0_3_pin6[1]), .pin3(1'b0),
    .pin4(cmp2_paddle_plus40_bits_0_3_pin4), .pin5(1'b0), .pin6(cmp2_paddle_plus40_bits_0_3_pin6[0]),
    .pin7(1'b1), .pin8(1'b0), .pin9(paddle_down), .pin10(paddle_down), .pin11(paddle_down),
    .pin12(paddle_down), .pin13(paddle_down), .pin14(1'b0), .pin15(cmp2_paddle_plus40_bits_0_3_pin6[2]),
    .pin16(1'b1));
  _7485 cmp2_xscan_lt_padright_bits_0_3 (
    .pin1(paddle_down), .pin2(cmp2_xscan_lt_padright_bits_0_3_pin2[0]),
    .pin3(cmp2_xscan_lt_padright_bits_0_3_pin2[1]), .pin4(cmp2_xscan_lt_padright_bits_0_3_pin2[2]),
    .pin5(cmp2_xscan_lt_padright_bits_0_3_pin5), .pin6(cmp2_xscan_lt_padright_bits_0_3_pin6),
    .pin7(cmp2_xscan_lt_padright_bits_0_3_pin7), .pin8(1'b0), .pin9(cmp2_paddle_plus40_bits_0_3_pin4),
    .pin10(paddle_down), .pin11(cmp2_paddle_plus40_bits_0_3_pin1), .pin12(paddle_down), .pin13(paddle_down),
    .pin14(paddle_down), .pin15(paddle_down), .pin16(paddle_down));
  _7485 ycmp1_gt460_bits_0_3 (
    .pin1(ycmp1_gt460_bits_0_3_pin9[3]), .pin2(ycmp1_gt460_bits_0_3_pin2[0]),
    .pin3(ycmp1_gt460_bits_0_3_pin2[1]), .pin4(ycmp1_gt460_bits_0_3_pin2[2]),
    .pin5(ycmp1_gt460_bits_0_3_pin5), .pin6(ycmp1_gt460_bits_0_3_pin6), .pin7(ycmp1_gt460_bits_0_3_pin7),
    .pin8(1'b0), .pin9(ycmp1_gt460_bits_0_3_pin9[0]), .pin10(1'b0), .pin11(ycmp1_gt460_bits_0_3_pin9[1]),
    .pin12(1'b0), .pin13(1'b0), .pin14(ycmp1_gt460_bits_0_3_pin9[2]), .pin15(1'b0), .pin16(1'b1));
  _7485 ycmp2_lt475_bits_0_3 (
    .pin1(ycmp2_lt475_bits_0_3_pin9[3]), .pin2(ycmp2_lt475_bits_0_3_pin2[0]),
    .pin3(ycmp2_lt475_bits_0_3_pin2[1]), .pin4(ycmp2_lt475_bits_0_3_pin2[2]),
    .pin5(ycmp2_lt475_bits_0_3_pin5), .pin6(ycmp2_lt475_bits_0_3_pin6), .pin7(ycmp2_lt475_bits_0_3_pin7),
    .pin8(1'b0), .pin9(ycmp2_lt475_bits_0_3_pin9[0]), .pin10(1'b0), .pin11(ycmp2_lt475_bits_0_3_pin9[1]),
    .pin12(1'b0), .pin13(1'b0), .pin14(ycmp2_lt475_bits_0_3_pin9[2]), .pin15(1'b0), .pin16(1'b1));
  _7485 cmp1_xscan_gt_pad40_bits_4_7 (
    .pin1(paddle_down), .pin2(cmp1_xscan_gt_pad40_bits_0_3_pin7), .pin3(cmp1_xscan_gt_pad40_bits_0_3_pin6),
    .pin4(cmp1_xscan_gt_pad40_bits_0_3_pin5), .pin5(cmp1_xscan_gt_pad40_bits_4_7_pin5),
    .pin6(cmp1_xscan_gt_pad40_bits_4_7_pin6), .pin7(cmp1_xscan_gt_pad40_bits_4_7_pin7), .pin8(1'b0),
    .pin9(paddle_down), .pin10(paddle_down), .pin11(paddle_down), .pin12(paddle_down), .pin13(paddle_down),
    .pin14(paddle_down), .pin15(paddle_down), .pin16(1'b1));
  _74283 cmp2_paddle_plus40_bits_4_7 (
    .pin1(cmp2_paddle_plus40_bits_4_7_pin1), .pin2(cmp2_paddle_plus40_bits_0_3_pin6[5]), .pin3(paddle_down),
    .pin4(cmp2_paddle_plus40_bits_4_7_pin4), .pin5(paddle_down), .pin6(cmp2_paddle_plus40_bits_0_3_pin6[4]),
    .pin7(paddle_down), .pin8(1'b0), .pin9(paddle_down), .pin10(paddle_down), .pin11(paddle_down),
    .pin12(paddle_down), .pin13(paddle_down), .pin14(paddle_down),
    .pin15(cmp2_paddle_plus40_bits_0_3_pin6[6]), .pin16(1'b1));
  _7485 cmp2_xscan_lt_padright_bits_4_7 (
    .pin1(paddle_down), .pin2(cmp2_xscan_lt_padright_bits_0_3_pin7),
    .pin3(cmp2_xscan_lt_padright_bits_0_3_pin6), .pin4(cmp2_xscan_lt_padright_bits_0_3_pin5),
    .pin5(cmp2_xscan_lt_padright_bits_4_7_pin5), .pin6(cmp2_xscan_lt_padright_bits_4_7_pin6),
    .pin7(cmp2_xscan_lt_padright_bits_4_7_pin7), .pin8(1'b0), .pin9(cmp2_paddle_plus40_bits_4_7_pin4),
    .pin10(paddle_down), .pin11(cmp2_paddle_plus40_bits_4_7_pin1), .pin12(paddle_down), .pin13(paddle_down),
    .pin14(paddle_down), .pin15(paddle_down), .pin16(paddle_down));
  _7485 ycmp1_gt460_bits_4_7 (
    .pin1(ycmp1_gt460_bits_0_3_pin9[7]), .pin2(ycmp1_gt460_bits_0_3_pin7), .pin3(ycmp1_gt460_bits_0_3_pin6),
    .pin4(ycmp1_gt460_bits_0_3_pin5), .pin5(ycmp1_gt460_bits_4_7_pin5), .pin6(ycmp1_gt460_bits_4_7_pin6),
    .pin7(ycmp1_gt460_bits_4_7_pin7), .pin8(1'b0), .pin9(ycmp1_gt460_bits_0_3_pin9[4]), .pin10(1'b0),
    .pin11(ycmp1_gt460_bits_0_3_pin9[5]), .pin12(1'b0), .pin13(1'b0), .pin14(ycmp1_gt460_bits_0_3_pin9[6]),
    .pin15(1'b0), .pin16(1'b1));
  _7485 ycmp2_lt475_bits_4_7 (
    .pin1(ycmp2_lt475_bits_0_3_pin9[7]), .pin2(ycmp2_lt475_bits_0_3_pin7), .pin3(ycmp2_lt475_bits_0_3_pin6),
    .pin4(ycmp2_lt475_bits_0_3_pin5), .pin5(ycmp2_lt475_bits_4_7_pin5), .pin6(ycmp2_lt475_bits_4_7_pin6),
    .pin7(ycmp2_lt475_bits_4_7_pin7), .pin8(1'b0), .pin9(ycmp2_lt475_bits_0_3_pin9[4]), .pin10(1'b0),
    .pin11(ycmp2_lt475_bits_0_3_pin9[5]), .pin12(1'b0), .pin13(1'b0), .pin14(ycmp2_lt475_bits_0_3_pin9[6]),
    .pin15(1'b0), .pin16(1'b1));
  _7485 cmp1_xscan_gt_pad40_bits_8_11 (
    .pin1(1'b0), .pin2(cmp1_xscan_gt_pad40_bits_4_7_pin7), .pin3(cmp1_xscan_gt_pad40_bits_4_7_pin6),
    .pin4(cmp1_xscan_gt_pad40_bits_4_7_pin5), .pin5(x_scan_b8), .pin8(1'b0), .pin9(x_paddle_px_b8),
    .pin10(x_scan_b8), .pin11(x_paddle_px_b9), .pin12(x_scan_b8), .pin13(1'b0), .pin14(1'b0), .pin15(1'b0),
    .pin16(1'b1));  // open: pin6, pin7
  _74283 cmp2_paddle_plus40_bits_8_11 (
    .pin1(cmp2_paddle_plus40_bits_8_11_pin1), .pin2(cmp2_paddle_plus40_bits_0_3_pin6[9]),
    .pin3(x_paddle_px_b9), .pin4(cmp2_paddle_plus40_bits_8_11_pin4), .pin5(x_paddle_px_b8),
    .pin6(cmp2_paddle_plus40_bits_0_3_pin6[8]), .pin7(paddle_down), .pin8(1'b0), .pin10(1'b1), .pin11(1'b1),
    .pin12(1'b1), .pin13(1'b1), .pin14(1'b1), .pin15(cmp2_paddle_plus40_bits_0_3_pin6[10]), .pin16(1'b1));  // open: pin9
  _7485 cmp2_xscan_lt_padright_bits_8_11 (
    .pin1(1'b1), .pin2(cmp2_xscan_lt_padright_bits_4_7_pin7), .pin3(cmp2_xscan_lt_padright_bits_4_7_pin6),
    .pin4(cmp2_xscan_lt_padright_bits_4_7_pin5), .pin7(x_scan_b8), .pin8(1'b0),
    .pin9(cmp2_paddle_plus40_bits_8_11_pin4), .pin10(x_scan_b8), .pin11(cmp2_paddle_plus40_bits_8_11_pin1),
    .pin12(x_scan_b8), .pin13(1'b1), .pin14(1'b1), .pin15(1'b1), .pin16(1'b1));  // open: pin5, pin6
  _7485 ycmp1_gt460_bits_8_11 (
    .pin1(ycmp1_gt460_bits_0_3_pin9[11]), .pin2(ycmp1_gt460_bits_4_7_pin7), .pin3(ycmp1_gt460_bits_4_7_pin6),
    .pin4(ycmp1_gt460_bits_4_7_pin5), .pin5(y_scan_b8), .pin8(1'b0), .pin9(ycmp1_gt460_bits_0_3_pin9[8]),
    .pin10(y_scan_b8), .pin11(ycmp1_gt460_bits_0_3_pin9[9]), .pin12(y_scan_b8), .pin13(1'b0),
    .pin14(ycmp1_gt460_bits_0_3_pin9[10]), .pin15(1'b0), .pin16(1'b1));  // open: pin6, pin7
  _7485 ycmp2_lt475_bits_8_11 (
    .pin1(ycmp2_lt475_bits_0_3_pin9[11]), .pin2(ycmp2_lt475_bits_4_7_pin7), .pin3(ycmp2_lt475_bits_4_7_pin6),
    .pin4(ycmp2_lt475_bits_4_7_pin5), .pin7(y_scan_b8), .pin8(1'b0), .pin9(ycmp2_lt475_bits_0_3_pin9[8]),
    .pin10(y_scan_b8), .pin11(ycmp2_lt475_bits_0_3_pin9[9]), .pin12(y_scan_b8), .pin13(1'b0),
    .pin14(ycmp2_lt475_bits_0_3_pin9[10]), .pin15(1'b0), .pin16(1'b1));  // open: pin5, pin6
  and PADDLE_X_WINDOW_AND (paddle_x_visible, x_scan_b8, x_scan_b8);
  and PADDLE_Y_WINDOW_AND (paddle_y_visible, y_scan_b8, y_scan_b8);
  and PADDLE_XY_FINAL_AND (PADDLE_XY_FINAL_AND_out, paddle_x_visible, paddle_y_visible);
  or FINAL_OR (final_or_out, 1'b0, PADDLE_XY_FINAL_AND_out);

  assign final_or_times100_b0 = 1'b0;
  assign final_or_times100_b1 = 1'b0;
  assign final_or_times100_b2 = final_or_out;
  assign final_or_times100_b3 = 1'b0;
  assign final_or_times100_b4 = 1'b0;
  assign final_or_times100_b5 = final_or_out;
  assign final_or_times100_b6 = final_or_out;
  assign paddle_d0 = paddle_down;
  assign paddle_d1 = paddle_down;
  assign paddle_d2 = paddle_down;
  assign paddle_d3 = paddle_down;
  assign paddle_up = paddle_down;
  assign x_paddle_px_b0 = 1'b0;
  assign x_paddle_px_b1 = 1'b0;
  assign x_paddle_px_b2 = 1'b0;
  assign x_paddle_px_b3 = paddle_down;
  assign x_paddle_px_b4 = paddle_down;
  assign x_paddle_px_b5 = paddle_down;
  assign x_paddle_px_b6 = paddle_down;
  assign x_paddle_px_b7 = paddle_down;
  assign x_scan_b0 = paddle_down;
  assign x_scan_b1 = paddle_down;
  assign x_scan_b2 = paddle_down;
  assign x_scan_b3 = paddle_down;
  assign x_scan_b4 = paddle_down;
  assign x_scan_b5 = paddle_down;
  assign x_scan_b6 = paddle_down;
  assign x_scan_b7 = paddle_down;
  assign x_scan_b9 = x_scan_b8;
  assign x_scan_eq_4 = paddle_down;
  assign x_scan_eq_6 = paddle_down;
  assign x_scan_eq_8 = paddle_down;
  assign x_scan_gt_paddle_x40 = x_scan_b8;
  assign x_scan_lt_8 = 1'b1;
  assign x_scan_lt_paddle_x40_plus40 = x_scan_b8;
  assign y_scan_b0 = 1'b0;
  assign y_scan_b1 = 1'b0;
  assign y_scan_b2 = 1'b0;
  assign y_scan_b3 = 1'b0;
  assign y_scan_b4 = 1'b0;
  assign y_scan_b5 = 1'b0;
  assign y_scan_b6 = 1'b0;
  assign y_scan_b7 = 1'b0;
  assign y_scan_b9 = y_scan_b8;
  assign y_scan_eq_4 = 1'b0;
  assign y_scan_eq_6 = 1'b0;
  assign y_scan_eq_8 = 1'b0;
  assign y_scan_gt_460 = y_scan_b8;
  assign y_scan_lt_475 = y_scan_b8;
  // also tied to GND on the sheet: {cmp1_xscan_gt_pad40_bits_0_3_pin2[0], cmp1_xscan_gt_pad40_bits_0_3_pin2[2], cmp2_paddle_plus40_bits_0_3_pin6[0], cmp2_paddle_plus40_bits_0_3_pin6[1], cmp2_paddle_plus40_bits_0_3_pin6[2], cmp2_paddle_plus40_bits_0_3_pin6[4], cmp2_paddle_plus40_bits_0_3_pin6[6], cmp2_paddle_plus40_bits_0_3_pin6[8], cmp2_paddle_plus40_bits_0_3_pin6[9], cmp2_paddle_plus40_bits_0_3_pin6[10], cmp2_xscan_lt_padright_bits_0_3_pin2[0], cmp2_xscan_lt_padright_bits_0_3_pin2[2], ycmp1_gt460_bits_0_3_pin2[0], ycmp1_gt460_bits_0_3_pin2[2], ycmp1_gt460_bits_0_3_pin9[0], ycmp1_gt460_bits_0_3_pin9[1], ycmp1_gt460_bits_0_3_pin9[4], ycmp1_gt460_bits_0_3_pin9[5], ycmp1_gt460_bits_0_3_pin9[9], ycmp1_gt460_bits_0_3_pin9[10], ycmp1_gt460_bits_0_3_pin9[11], ycmp2_lt475_bits_0_3_pin2[0], ycmp2_lt475_bits_0_3_pin2[2], ycmp2_lt475_bits_0_3_pin9[2], ycmp2_lt475_bits_0_3_pin9[5], ycmp2_lt475_bits_0_3_pin9[9], ycmp2_lt475_bits_0_3_pin9[10], ycmp2_lt475_bits_0_3_pin9[11]}
  // also tied to VCC on the sheet: {cmp1_xscan_gt_pad40_bits_0_3_pin2[1], cmp2_paddle_plus40_bits_0_3_pin6[5], paddle_down, cmp2_xscan_lt_padright_bits_0_3_pin2[1], ycmp1_gt460_bits_0_3_pin2[1], ycmp1_gt460_bits_0_3_pin9[2], ycmp1_gt460_bits_0_3_pin9[3], ycmp1_gt460_bits_0_3_pin9[6], ycmp1_gt460_bits_0_3_pin9[7], ycmp1_gt460_bits_0_3_pin9[8], ycmp2_lt475_bits_0_3_pin2[1], ycmp2_lt475_bits_0_3_pin9[0], ycmp2_lt475_bits_0_3_pin9[1], ycmp2_lt475_bits_0_3_pin9[3], ycmp2_lt475_bits_0_3_pin9[4], ycmp2_lt475_bits_0_3_pin9[6], ycmp2_lt475_bits_0_3_pin9[7], ycmp2_lt475_bits_0_3_pin9[8], pixel_clock}

  // Notes on the sheet:
  //   X_Paddle
  //   PADDLE X × 40
  //   40·X = (X << 5) + (X << 3)
  //   uscita: 0, 40, 80, …, 600
  //   x_paddle_px[9:0]
  //   TEST_START = 4
  //   10 bit: 0000000100
  //   4 stored as a 12-bit constant: 0000 0000 0100
  //   TEST_END = 6
  //   10 bit: 0000000110
  //   6 stored as a 12-bit constant: 0000 0000 0110
  //   TEST_LINE_END = 8
  //   12 bit: 0000 0000 1000
  //   Y clock: fronte di salita di x_scan_lt_8 (una volta per riga di prova)
  //   TEST_FRAME_END = 8
  //   X_SCAN COUNTER (10 bit usati)
  //   Y_SCAN COUNTER (10 bit usati)
  //   X_SCAN vs TEST_START
  //   X_SCAN vs TEST_END
  //   X_SCAN vs TEST_LINE_END
  //   Y_SCAN vs TEST_START
  //   Y_SCAN vs TEST_END
  //   Y_SCAN vs TEST_FRAME_END
  //   X_SCAN > X_PADDLE × 40
  //   X_PADDLE × 40 + 40
  //   X_SCAN < X_PADDLE × 40 + 40
  //   Y_SCAN > 460
  //   Y_SCAN < 475
  //   FINAL_OR × 100 = S·1100100₂
endmodule
