// Digital circuit circuit_test_with_final_or.dig as structural Verilog
module circuit_test_with_final_or (
  input  paddle_down,
  input  paddle_up,
  input  paddle_load_n,
  input  paddle_clear,
  input  paddle_q2_in,
  input  paddle_q3_in,
  input  paddle_q1_in,
  input  paddle_q0_in,
  input  pixel_clock,
  output paddle_d0,
  output paddle_d1,
  output paddle_d2,
  output paddle_d3,
  output paddle_borrow_out,
  output paddle_carry_out,
  output x_scan_b0,
  output x_scan_b1,
  output x_scan_b2,
  output x_scan_b3,
  output x_scan_b4,
  output x_scan_b5,
  output x_scan_b6,
  output x_scan_b7,
  output x_scan_b8,
  output x_scan_b9,
  output x_scan_gt_4,
  output x_scan_eq_4,
  output x_scan_lt_4,
  output x_scan_gt_6,
  output x_scan_eq_6,
  output x_scan_lt_6,
  output hsync_n,
  output x_scan_gt_8,
  output x_scan_eq_8,
  output x_scan_lt_8,
  output x_scan_clear_n,
  output y_scan_b0,
  output y_scan_b1,
  output y_scan_b2,
  output y_scan_b3,
  output y_scan_b4,
  output y_scan_b5,
  output y_scan_b6,
  output y_scan_b7,
  output y_scan_b8,
  output y_scan_b9,
  output y_scan_gt_4,
  output y_scan_eq_4,
  output y_scan_lt_4,
  output y_scan_gt_6,
  output y_scan_eq_6,
  output y_scan_lt_6,
  output vsync_n,
  output y_scan_gt_8,
  output y_scan_eq_8,
  output y_scan_lt_8,
  output y_scan_clear_n,
  output paddle_x_visible,
  output paddle_y_visible,
  output paddle_visible,
  output final_or_out
);

  wire PADPLUS40_ADD_0_pin1, PADPLUS40_ADD_0_pin4, PADPLUS40_ADD_0_pin9, PADPLUS40_ADD_0_pin10,
       PADPLUS40_ADD_0_pin13, PADPLUS40_ADD_1_pin1, PADPLUS40_ADD_1_pin4, PADPLUS40_ADD_1_pin9,
       PADPLUS40_ADD_1_pin10, PADPLUS40_ADD_1_pin13, PADPLUS40_ADD_2_pin1, PADPLUS40_ADD_2_pin4,
       PADPLUS40_ADD_2_pin10, PADPLUS40_ADD_2_pin13, x_paddle_times_40_adder_clean_pin1,
       x_paddle_times_40_adder_clean_pin4, x_paddle_times_40_adder_clean_pin9,
       x_paddle_times_40_adder_clean_pin10, x_paddle_times_40_adder_clean_pin13, x_scan_cmp4_bits_0_3_pin5,
       x_scan_cmp4_bits_0_3_pin6, x_scan_cmp4_bits_0_3_pin7, x_scan_cmp4_bits_4_7_pin5,
       x_scan_cmp4_bits_4_7_pin6, x_scan_cmp4_bits_4_7_pin7, x_scan_cmp6_bits_0_3_pin5,
       x_scan_cmp6_bits_0_3_pin6, x_scan_cmp6_bits_0_3_pin7, x_scan_cmp6_bits_4_7_pin5,
       x_scan_cmp6_bits_4_7_pin6, x_scan_cmp6_bits_4_7_pin7, x_scan_cmp8_bits_0_3_pin5,
       x_scan_cmp8_bits_0_3_pin6, x_scan_cmp8_bits_0_3_pin7, x_scan_cmp8_bits_4_7_pin5,
       x_scan_cmp8_bits_4_7_pin6, x_scan_cmp8_bits_4_7_pin7, x_scan_counter_bits_0_3_pin15,
       x_scan_counter_bits_4_7_pin15, x_scan_counter_bits_8_11_pin11, x_scan_counter_bits_8_11_pin12,
       XGT_PAD_CMP_0_pin5, XGT_PAD_CMP_0_pin6, XGT_PAD_CMP_0_pin7, XGT_PAD_CMP_1_pin5, XGT_PAD_CMP_1_pin6,
       XGT_PAD_CMP_1_pin7, XGT_PAD_CMP_2_pin5, XLT_PADRIGHT_CMP_0_pin5, XLT_PADRIGHT_CMP_0_pin6,
       XLT_PADRIGHT_CMP_0_pin7, XLT_PADRIGHT_CMP_1_pin5, XLT_PADRIGHT_CMP_1_pin6, XLT_PADRIGHT_CMP_1_pin7,
       XLT_PADRIGHT_CMP_2_pin5, y_scan_cmp4_bits_0_3_pin5, y_scan_cmp4_bits_0_3_pin6,
       y_scan_cmp4_bits_0_3_pin7, y_scan_cmp4_bits_4_7_pin5, y_scan_cmp4_bits_4_7_pin6,
       y_scan_cmp4_bits_4_7_pin7, y_scan_cmp6_bits_0_3_pin5, y_scan_cmp6_bits_0_3_pin6,
       y_scan_cmp6_bits_0_3_pin7, y_scan_cmp6_bits_4_7_pin5, y_scan_cmp6_bits_4_7_pin6,
       y_scan_cmp6_bits_4_7_pin7, y_scan_cmp8_bits_0_3_pin5, y_scan_cmp8_bits_0_3_pin6,
       y_scan_cmp8_bits_0_3_pin7, y_scan_cmp8_bits_4_7_pin5, y_scan_cmp8_bits_4_7_pin6,
       y_scan_cmp8_bits_4_7_pin7, y_scan_counter_bits_0_3_pin15, y_scan_counter_bits_4_7_pin15,
       y_scan_counter_bits_8_11_pin11, y_scan_counter_bits_8_11_pin12, YGT460_CMP_0_pin5, YGT460_CMP_0_pin6,
       YGT460_CMP_0_pin7, YGT460_CMP_1_pin5, YGT460_CMP_1_pin6, YGT460_CMP_1_pin7, YGT460_CMP_2_pin5,
       YLT475_CMP_0_pin5, YLT475_CMP_0_pin6, YLT475_CMP_0_pin7, YLT475_CMP_1_pin5, YLT475_CMP_1_pin6,
       YLT475_CMP_1_pin7, YLT475_CMP_2_pin7;
  wire [2:0] x_scan_cmp4_bits_0_3_pin2, x_scan_cmp6_bits_0_3_pin2, x_scan_cmp8_bits_0_3_pin2,
       y_scan_cmp4_bits_0_3_pin2, y_scan_cmp6_bits_0_3_pin2, y_scan_cmp8_bits_0_3_pin2;
  wire [11:0] x_scan_cmp4_bits_0_3_pin9, x_scan_cmp6_bits_0_3_pin9, x_scan_cmp8_bits_0_3_pin9,
       y_scan_cmp4_bits_0_3_pin9, y_scan_cmp6_bits_0_3_pin9, y_scan_cmp8_bits_0_3_pin9;

  _74193 x_paddle_counter (
    .pin1(paddle_load_n), .pin2(paddle_d2), .pin3(paddle_d3), .pin4(paddle_down), .pin5(paddle_up),
    .pin6(paddle_d1), .pin7(paddle_d0), .pin8(1'b0), .pin9(paddle_q3_in), .pin10(paddle_q2_in),
    .pin11(paddle_q1_in), .pin12(paddle_borrow_out), .pin13(paddle_carry_out), .pin14(paddle_q0_in),
    .pin15(paddle_clear), .pin16(1'b1));
  _74163 x_scan_counter_bits_0_3 (
    .pin1(x_scan_clear_n), .pin2(pixel_clock), .pin3(1'b0), .pin4(1'b0), .pin5(1'b0), .pin6(1'b0),
    .pin7(1'b1), .pin8(1'b0), .pin9(1'b1), .pin10(1'b1), .pin11(x_scan_b3), .pin12(x_scan_b2),
    .pin13(x_scan_b1), .pin14(x_scan_b0), .pin15(x_scan_counter_bits_0_3_pin15), .pin16(1'b1));
  _74163 y_scan_counter_bits_0_3 (
    .pin1(y_scan_clear_n), .pin2(x_scan_clear_n), .pin3(1'b0), .pin4(1'b0), .pin5(1'b0), .pin6(1'b0),
    .pin7(1'b1), .pin8(1'b0), .pin9(1'b1), .pin10(1'b1), .pin11(y_scan_b3), .pin12(y_scan_b2),
    .pin13(y_scan_b1), .pin14(y_scan_b0), .pin15(y_scan_counter_bits_0_3_pin15), .pin16(1'b1));
  _7485 x_scan_cmp4_bits_0_3 (
    .pin1(x_scan_cmp4_bits_0_3_pin9[3]), .pin2(x_scan_cmp4_bits_0_3_pin2[0]),
    .pin3(x_scan_cmp4_bits_0_3_pin2[1]), .pin4(x_scan_cmp4_bits_0_3_pin2[2]),
    .pin5(x_scan_cmp4_bits_0_3_pin5), .pin6(x_scan_cmp4_bits_0_3_pin6), .pin7(x_scan_cmp4_bits_0_3_pin7),
    .pin8(1'b0), .pin9(x_scan_cmp4_bits_0_3_pin9[0]), .pin10(x_scan_b0),
    .pin11(x_scan_cmp4_bits_0_3_pin9[1]), .pin12(x_scan_b1), .pin13(x_scan_b2),
    .pin14(x_scan_cmp4_bits_0_3_pin9[2]), .pin15(x_scan_b3), .pin16(1'b1));
  _7485 x_scan_cmp6_bits_0_3 (
    .pin1(x_scan_cmp6_bits_0_3_pin9[3]), .pin2(x_scan_cmp6_bits_0_3_pin2[0]),
    .pin3(x_scan_cmp6_bits_0_3_pin2[1]), .pin4(x_scan_cmp6_bits_0_3_pin2[2]),
    .pin5(x_scan_cmp6_bits_0_3_pin5), .pin6(x_scan_cmp6_bits_0_3_pin6), .pin7(x_scan_cmp6_bits_0_3_pin7),
    .pin8(1'b0), .pin9(x_scan_cmp6_bits_0_3_pin9[0]), .pin10(x_scan_b0),
    .pin11(x_scan_cmp6_bits_0_3_pin9[1]), .pin12(x_scan_b1), .pin13(x_scan_b2),
    .pin14(x_scan_cmp6_bits_0_3_pin9[2]), .pin15(x_scan_b3), .pin16(1'b1));
  _7485 x_scan_cmp8_bits_0_3 (
    .pin1(x_scan_cmp8_bits_0_3_pin9[3]), .pin2(x_scan_cmp8_bits_0_3_pin2[0]),
    .pin3(x_scan_cmp8_bits_0_3_pin2[1]), .pin4(x_scan_cmp8_bits_0_3_pin2[2]),
    .pin5(x_scan_cmp8_bits_0_3_pin5), .pin6(x_scan_cmp8_bits_0_3_pin6), .pin7(x_scan_cmp8_bits_0_3_pin7),
    .pin8(1'b0), .pin9(x_scan_cmp8_bits_0_3_pin9[0]), .pin10(x_scan_b0),
    .pin11(x_scan_cmp8_bits_0_3_pin9[1]), .pin12(x_scan_b1), .pin13(x_scan_b2),
    .pin14(x_scan_cmp8_bits_0_3_pin9[2]), .pin15(x_scan_b3), .pin16(1'b1));
  _7485 y_scan_cmp4_bits_0_3 (
    .pin1(y_scan_cmp4_bits_0_3_pin9[3]), .pin2(y_scan_cmp4_bits_0_3_pin2[0]),
    .pin3(y_scan_cmp4_bits_0_3_pin2[1]), .pin4(y_scan_cmp4_bits_0_3_pin2[2]),
    .pin5(y_scan_cmp4_bits_0_3_pin5), .pin6(y_scan_cmp4_bits_0_3_pin6), .pin7(y_scan_cmp4_bits_0_3_pin7),
    .pin8(1'b0), .pin9(y_scan_cmp4_bits_0_3_pin9[0]), .pin10(y_scan_b0),
    .pin11(y_scan_cmp4_bits_0_3_pin9[1]), .pin12(y_scan_b1), .pin13(y_scan_b2),
    .pin14(y_scan_cmp4_bits_0_3_pin9[2]), .pin15(y_scan_b3), .pin16(1'b1));
  _7485 y_scan_cmp6_bits_0_3 (
    .pin1(y_scan_cmp6_bits_0_3_pin9[3]), .pin2(y_scan_cmp6_bits_0_3_pin2[0]),
    .pin3(y_scan_cmp6_bits_0_3_pin2[1]), .pin4(y_scan_cmp6_bits_0_3_pin2[2]),
    .pin5(y_scan_cmp6_bits_0_3_pin5), .pin6(y_scan_cmp6_bits_0_3_pin6), .pin7(y_scan_cmp6_bits_0_3_pin7),
    .pin8(1'b0), .pin9(y_scan_cmp6_bits_0_3_pin9[0]), .pin10(y_scan_b0),
    .pin11(y_scan_cmp6_bits_0_3_pin9[1]), .pin12(y_scan_b1), .pin13(y_scan_b2),
    .pin14(y_scan_cmp6_bits_0_3_pin9[2]), .pin15(y_scan_b3), .pin16(1'b1));
  _7485 y_scan_cmp8_bits_0_3 (
    .pin1(y_scan_cmp8_bits_0_3_pin9[3]), .pin2(y_scan_cmp8_bits_0_3_pin2[0]),
    .pin3(y_scan_cmp8_bits_0_3_pin2[1]), .pin4(y_scan_cmp8_bits_0_3_pin2[2]),
    .pin5(y_scan_cmp8_bits_0_3_pin5), .pin6(y_scan_cmp8_bits_0_3_pin6), .pin7(y_scan_cmp8_bits_0_3_pin7),
    .pin8(1'b0), .pin9(y_scan_cmp8_bits_0_3_pin9[0]), .pin10(y_scan_b0),
    .pin11(y_scan_cmp8_bits_0_3_pin9[1]), .pin12(y_scan_b1), .pin13(y_scan_b2),
    .pin14(y_scan_cmp8_bits_0_3_pin9[2]), .pin15(y_scan_b3), .pin16(1'b1));
  _74163 x_scan_counter_bits_4_7 (
    .pin1(x_scan_clear_n), .pin2(pixel_clock), .pin3(1'b0), .pin4(1'b0), .pin5(1'b0), .pin6(1'b0),
    .pin7(1'b1), .pin8(1'b0), .pin9(1'b1), .pin10(x_scan_counter_bits_0_3_pin15), .pin11(x_scan_b7),
    .pin12(x_scan_b6), .pin13(x_scan_b5), .pin14(x_scan_b4), .pin15(x_scan_counter_bits_4_7_pin15),
    .pin16(1'b1));
  _74163 y_scan_counter_bits_4_7 (
    .pin1(y_scan_clear_n), .pin2(x_scan_clear_n), .pin3(1'b0), .pin4(1'b0), .pin5(1'b0), .pin6(1'b0),
    .pin7(1'b1), .pin8(1'b0), .pin9(1'b1), .pin10(y_scan_counter_bits_0_3_pin15), .pin11(y_scan_b7),
    .pin12(y_scan_b6), .pin13(y_scan_b5), .pin14(y_scan_b4), .pin15(y_scan_counter_bits_4_7_pin15),
    .pin16(1'b1));
  _7485 x_scan_cmp4_bits_4_7 (
    .pin1(x_scan_cmp4_bits_0_3_pin9[7]), .pin2(x_scan_cmp4_bits_0_3_pin7), .pin3(x_scan_cmp4_bits_0_3_pin6),
    .pin4(x_scan_cmp4_bits_0_3_pin5), .pin5(x_scan_cmp4_bits_4_7_pin5), .pin6(x_scan_cmp4_bits_4_7_pin6),
    .pin7(x_scan_cmp4_bits_4_7_pin7), .pin8(1'b0), .pin9(x_scan_cmp4_bits_0_3_pin9[4]), .pin10(x_scan_b4),
    .pin11(x_scan_cmp4_bits_0_3_pin9[5]), .pin12(x_scan_b5), .pin13(x_scan_b6),
    .pin14(x_scan_cmp4_bits_0_3_pin9[6]), .pin15(x_scan_b7), .pin16(1'b1));
  _7485 x_scan_cmp6_bits_4_7 (
    .pin1(x_scan_cmp6_bits_0_3_pin9[7]), .pin2(x_scan_cmp6_bits_0_3_pin7), .pin3(x_scan_cmp6_bits_0_3_pin6),
    .pin4(x_scan_cmp6_bits_0_3_pin5), .pin5(x_scan_cmp6_bits_4_7_pin5), .pin6(x_scan_cmp6_bits_4_7_pin6),
    .pin7(x_scan_cmp6_bits_4_7_pin7), .pin8(1'b0), .pin9(x_scan_cmp6_bits_0_3_pin9[4]), .pin10(x_scan_b4),
    .pin11(x_scan_cmp6_bits_0_3_pin9[5]), .pin12(x_scan_b5), .pin13(x_scan_b6),
    .pin14(x_scan_cmp6_bits_0_3_pin9[6]), .pin15(x_scan_b7), .pin16(1'b1));
  _7485 x_scan_cmp8_bits_4_7 (
    .pin1(x_scan_cmp8_bits_0_3_pin9[7]), .pin2(x_scan_cmp8_bits_0_3_pin7), .pin3(x_scan_cmp8_bits_0_3_pin6),
    .pin4(x_scan_cmp8_bits_0_3_pin5), .pin5(x_scan_cmp8_bits_4_7_pin5), .pin6(x_scan_cmp8_bits_4_7_pin6),
    .pin7(x_scan_cmp8_bits_4_7_pin7), .pin8(1'b0), .pin9(x_scan_cmp8_bits_0_3_pin9[4]), .pin10(x_scan_b4),
    .pin11(x_scan_cmp8_bits_0_3_pin9[5]), .pin12(x_scan_b5), .pin13(x_scan_b6),
    .pin14(x_scan_cmp8_bits_0_3_pin9[6]), .pin15(x_scan_b7), .pin16(1'b1));
  _7485 y_scan_cmp4_bits_4_7 (
    .pin1(y_scan_cmp4_bits_0_3_pin9[7]), .pin2(y_scan_cmp4_bits_0_3_pin7), .pin3(y_scan_cmp4_bits_0_3_pin6),
    .pin4(y_scan_cmp4_bits_0_3_pin5), .pin5(y_scan_cmp4_bits_4_7_pin5), .pin6(y_scan_cmp4_bits_4_7_pin6),
    .pin7(y_scan_cmp4_bits_4_7_pin7), .pin8(1'b0), .pin9(y_scan_cmp4_bits_0_3_pin9[4]), .pin10(y_scan_b4),
    .pin11(y_scan_cmp4_bits_0_3_pin9[5]), .pin12(y_scan_b5), .pin13(y_scan_b6),
    .pin14(y_scan_cmp4_bits_0_3_pin9[6]), .pin15(y_scan_b7), .pin16(1'b1));
  _7485 y_scan_cmp6_bits_4_7 (
    .pin1(y_scan_cmp6_bits_0_3_pin9[7]), .pin2(y_scan_cmp6_bits_0_3_pin7), .pin3(y_scan_cmp6_bits_0_3_pin6),
    .pin4(y_scan_cmp6_bits_0_3_pin5), .pin5(y_scan_cmp6_bits_4_7_pin5), .pin6(y_scan_cmp6_bits_4_7_pin6),
    .pin7(y_scan_cmp6_bits_4_7_pin7), .pin8(1'b0), .pin9(y_scan_cmp6_bits_0_3_pin9[4]), .pin10(y_scan_b4),
    .pin11(y_scan_cmp6_bits_0_3_pin9[5]), .pin12(y_scan_b5), .pin13(y_scan_b6),
    .pin14(y_scan_cmp6_bits_0_3_pin9[6]), .pin15(y_scan_b7), .pin16(1'b1));
  _7485 y_scan_cmp8_bits_4_7 (
    .pin1(y_scan_cmp8_bits_0_3_pin9[7]), .pin2(y_scan_cmp8_bits_0_3_pin7), .pin3(y_scan_cmp8_bits_0_3_pin6),
    .pin4(y_scan_cmp8_bits_0_3_pin5), .pin5(y_scan_cmp8_bits_4_7_pin5), .pin6(y_scan_cmp8_bits_4_7_pin6),
    .pin7(y_scan_cmp8_bits_4_7_pin7), .pin8(1'b0), .pin9(y_scan_cmp8_bits_0_3_pin9[4]), .pin10(y_scan_b4),
    .pin11(y_scan_cmp8_bits_0_3_pin9[5]), .pin12(y_scan_b5), .pin13(y_scan_b6),
    .pin14(y_scan_cmp8_bits_0_3_pin9[6]), .pin15(y_scan_b7), .pin16(1'b1));
  _74163 x_scan_counter_bits_8_11 (
    .pin1(x_scan_clear_n), .pin2(pixel_clock), .pin3(1'b0), .pin4(1'b0), .pin5(1'b0), .pin6(1'b0),
    .pin7(1'b1), .pin8(1'b0), .pin9(1'b1), .pin10(x_scan_counter_bits_4_7_pin15),
    .pin11(x_scan_counter_bits_8_11_pin11), .pin12(x_scan_counter_bits_8_11_pin12), .pin13(x_scan_b9),
    .pin14(x_scan_b8), .pin16(1'b1));  // open: pin15
  _74163 y_scan_counter_bits_8_11 (
    .pin1(y_scan_clear_n), .pin2(x_scan_clear_n), .pin3(1'b0), .pin4(1'b0), .pin5(1'b0), .pin6(1'b0),
    .pin7(1'b1), .pin8(1'b0), .pin9(1'b1), .pin10(y_scan_counter_bits_4_7_pin15),
    .pin11(y_scan_counter_bits_8_11_pin11), .pin12(y_scan_counter_bits_8_11_pin12), .pin13(y_scan_b9),
    .pin14(y_scan_b8), .pin16(1'b1));  // open: pin15
  _7485 x_scan_cmp4_bits_8_11 (
    .pin1(x_scan_cmp4_bits_0_3_pin9[11]), .pin2(x_scan_cmp4_bits_4_7_pin7), .pin3(x_scan_cmp4_bits_4_7_pin6),
    .pin4(x_scan_cmp4_bits_4_7_pin5), .pin5(x_scan_gt_4), .pin6(x_scan_eq_4), .pin7(x_scan_lt_4),
    .pin8(1'b0), .pin9(x_scan_cmp4_bits_0_3_pin9[8]), .pin10(x_scan_b8),
    .pin11(x_scan_cmp4_bits_0_3_pin9[9]), .pin12(x_scan_b9), .pin13(x_scan_counter_bits_8_11_pin12),
    .pin14(x_scan_cmp4_bits_0_3_pin9[10]), .pin15(x_scan_counter_bits_8_11_pin11), .pin16(1'b1));
  _7485 x_scan_cmp6_bits_8_11 (
    .pin1(x_scan_cmp6_bits_0_3_pin9[11]), .pin2(x_scan_cmp6_bits_4_7_pin7), .pin3(x_scan_cmp6_bits_4_7_pin6),
    .pin4(x_scan_cmp6_bits_4_7_pin5), .pin5(x_scan_gt_6), .pin6(x_scan_eq_6), .pin7(x_scan_lt_6),
    .pin8(1'b0), .pin9(x_scan_cmp6_bits_0_3_pin9[8]), .pin10(x_scan_b8),
    .pin11(x_scan_cmp6_bits_0_3_pin9[9]), .pin12(x_scan_b9), .pin13(x_scan_counter_bits_8_11_pin12),
    .pin14(x_scan_cmp6_bits_0_3_pin9[10]), .pin15(x_scan_counter_bits_8_11_pin11), .pin16(1'b1));
  _7485 x_scan_cmp8_bits_8_11 (
    .pin1(x_scan_cmp8_bits_0_3_pin9[11]), .pin2(x_scan_cmp8_bits_4_7_pin7), .pin3(x_scan_cmp8_bits_4_7_pin6),
    .pin4(x_scan_cmp8_bits_4_7_pin5), .pin5(x_scan_gt_8), .pin6(x_scan_eq_8), .pin7(x_scan_clear_n),
    .pin8(1'b0), .pin9(x_scan_cmp8_bits_0_3_pin9[8]), .pin10(x_scan_b8),
    .pin11(x_scan_cmp8_bits_0_3_pin9[9]), .pin12(x_scan_b9), .pin13(x_scan_counter_bits_8_11_pin12),
    .pin14(x_scan_cmp8_bits_0_3_pin9[10]), .pin15(x_scan_counter_bits_8_11_pin11), .pin16(1'b1));
  _7485 y_scan_cmp4_bits_8_11 (
    .pin1(y_scan_cmp4_bits_0_3_pin9[11]), .pin2(y_scan_cmp4_bits_4_7_pin7), .pin3(y_scan_cmp4_bits_4_7_pin6),
    .pin4(y_scan_cmp4_bits_4_7_pin5), .pin5(y_scan_gt_4), .pin6(y_scan_eq_4), .pin7(y_scan_lt_4),
    .pin8(1'b0), .pin9(y_scan_cmp4_bits_0_3_pin9[8]), .pin10(y_scan_b8),
    .pin11(y_scan_cmp4_bits_0_3_pin9[9]), .pin12(y_scan_b9), .pin13(y_scan_counter_bits_8_11_pin12),
    .pin14(y_scan_cmp4_bits_0_3_pin9[10]), .pin15(y_scan_counter_bits_8_11_pin11), .pin16(1'b1));
  _7485 y_scan_cmp6_bits_8_11 (
    .pin1(y_scan_cmp6_bits_0_3_pin9[11]), .pin2(y_scan_cmp6_bits_4_7_pin7), .pin3(y_scan_cmp6_bits_4_7_pin6),
    .pin4(y_scan_cmp6_bits_4_7_pin5), .pin5(y_scan_gt_6), .pin6(y_scan_eq_6), .pin7(y_scan_lt_6),
    .pin8(1'b0), .pin9(y_scan_cmp6_bits_0_3_pin9[8]), .pin10(y_scan_b8),
    .pin11(y_scan_cmp6_bits_0_3_pin9[9]), .pin12(y_scan_b9), .pin13(y_scan_counter_bits_8_11_pin12),
    .pin14(y_scan_cmp6_bits_0_3_pin9[10]), .pin15(y_scan_counter_bits_8_11_pin11), .pin16(1'b1));
  _7485 y_scan_cmp8_bits_8_11 (
    .pin1(y_scan_cmp8_bits_0_3_pin9[11]), .pin2(y_scan_cmp8_bits_4_7_pin7), .pin3(y_scan_cmp8_bits_4_7_pin6),
    .pin4(y_scan_cmp8_bits_4_7_pin5), .pin5(y_scan_gt_8), .pin6(y_scan_eq_8), .pin7(y_scan_clear_n),
    .pin8(1'b0), .pin9(y_scan_cmp8_bits_0_3_pin9[8]), .pin10(y_scan_b8),
    .pin11(y_scan_cmp8_bits_0_3_pin9[9]), .pin12(y_scan_b9), .pin13(y_scan_counter_bits_8_11_pin12),
    .pin14(y_scan_cmp8_bits_0_3_pin9[10]), .pin15(y_scan_counter_bits_8_11_pin11), .pin16(1'b1));
  nand x_test_window_nand (hsync_n, x_scan_gt_4, x_scan_lt_6);
  nand y_test_window_nand (vsync_n, y_scan_gt_4, y_scan_lt_6);
  _74283 x_paddle_times_40_adder_clean (
    .pin1(x_paddle_times_40_adder_clean_pin1), .pin2(paddle_d0), .pin3(paddle_d2),
    .pin4(x_paddle_times_40_adder_clean_pin4), .pin5(paddle_d3), .pin6(paddle_d1), .pin7(1'b0), .pin8(1'b0),
    .pin9(x_paddle_times_40_adder_clean_pin9), .pin10(x_paddle_times_40_adder_clean_pin10), .pin11(1'b0),
    .pin12(paddle_d0), .pin13(x_paddle_times_40_adder_clean_pin13), .pin14(paddle_d1), .pin15(1'b0),
    .pin16(1'b1));
  _7485 XGT_PAD_CMP_0 (
    .pin1(paddle_d3), .pin2(1'b0), .pin3(1'b1), .pin4(1'b0), .pin5(XGT_PAD_CMP_0_pin5),
    .pin6(XGT_PAD_CMP_0_pin6), .pin7(XGT_PAD_CMP_0_pin7), .pin8(1'b0), .pin9(1'b0), .pin10(x_scan_b0),
    .pin11(1'b0), .pin12(x_scan_b1), .pin13(x_scan_b2), .pin14(1'b0), .pin15(x_scan_b3), .pin16(1'b1));
  _74283 PADPLUS40_ADD_0 (
    .pin1(PADPLUS40_ADD_0_pin1), .pin2(1'b0), .pin3(1'b0), .pin4(PADPLUS40_ADD_0_pin4), .pin5(1'b0),
    .pin6(1'b0), .pin7(1'b0), .pin8(1'b0), .pin9(PADPLUS40_ADD_0_pin9), .pin10(PADPLUS40_ADD_0_pin10),
    .pin11(1'b1), .pin12(paddle_d3), .pin13(PADPLUS40_ADD_0_pin13), .pin14(1'b0), .pin15(1'b0), .pin16(1'b1));
  _7485 XLT_PADRIGHT_CMP_0 (
    .pin1(x_scan_b3), .pin2(1'b0), .pin3(1'b1), .pin4(1'b0), .pin5(XLT_PADRIGHT_CMP_0_pin5),
    .pin6(XLT_PADRIGHT_CMP_0_pin6), .pin7(XLT_PADRIGHT_CMP_0_pin7), .pin8(1'b0), .pin9(x_scan_b0),
    .pin10(PADPLUS40_ADD_0_pin4), .pin11(x_scan_b1), .pin12(PADPLUS40_ADD_0_pin1),
    .pin13(PADPLUS40_ADD_0_pin13), .pin14(x_scan_b2), .pin15(PADPLUS40_ADD_0_pin10), .pin16(1'b1));
  _7485 YGT460_CMP_0 (
    .pin1(1'b1), .pin2(1'b0), .pin3(1'b1), .pin4(1'b0), .pin5(YGT460_CMP_0_pin5), .pin6(YGT460_CMP_0_pin6),
    .pin7(YGT460_CMP_0_pin7), .pin8(1'b0), .pin9(1'b0), .pin10(y_scan_b0), .pin11(1'b0), .pin12(y_scan_b1),
    .pin13(y_scan_b2), .pin14(1'b1), .pin15(y_scan_b3), .pin16(1'b1));
  _7485 YLT475_CMP_0 (
    .pin1(1'b1), .pin2(1'b0), .pin3(1'b1), .pin4(1'b0), .pin5(YLT475_CMP_0_pin5), .pin6(YLT475_CMP_0_pin6),
    .pin7(YLT475_CMP_0_pin7), .pin8(1'b0), .pin9(1'b1), .pin10(y_scan_b0), .pin11(1'b1), .pin12(y_scan_b1),
    .pin13(y_scan_b2), .pin14(1'b0), .pin15(y_scan_b3), .pin16(1'b1));
  _7485 XGT_PAD_CMP_1 (
    .pin1(x_paddle_times_40_adder_clean_pin13), .pin2(XGT_PAD_CMP_0_pin7), .pin3(XGT_PAD_CMP_0_pin6),
    .pin4(XGT_PAD_CMP_0_pin5), .pin5(XGT_PAD_CMP_1_pin5), .pin6(XGT_PAD_CMP_1_pin6),
    .pin7(XGT_PAD_CMP_1_pin7), .pin8(1'b0), .pin9(paddle_d2), .pin10(x_scan_b4),
    .pin11(x_paddle_times_40_adder_clean_pin4), .pin12(x_scan_b5), .pin13(x_scan_b6),
    .pin14(x_paddle_times_40_adder_clean_pin1), .pin15(x_scan_b7), .pin16(1'b1));
  _74283 PADPLUS40_ADD_1 (
    .pin1(PADPLUS40_ADD_1_pin1), .pin2(1'b1), .pin3(x_paddle_times_40_adder_clean_pin4),
    .pin4(PADPLUS40_ADD_1_pin4), .pin5(paddle_d2), .pin6(1'b0), .pin7(PADPLUS40_ADD_0_pin9), .pin8(1'b0),
    .pin9(PADPLUS40_ADD_1_pin9), .pin10(PADPLUS40_ADD_1_pin10), .pin11(1'b0),
    .pin12(x_paddle_times_40_adder_clean_pin13), .pin13(PADPLUS40_ADD_1_pin13),
    .pin14(x_paddle_times_40_adder_clean_pin1), .pin15(1'b0), .pin16(1'b1));
  _7485 XLT_PADRIGHT_CMP_1 (
    .pin1(x_scan_b7), .pin2(XLT_PADRIGHT_CMP_0_pin7), .pin3(XLT_PADRIGHT_CMP_0_pin6),
    .pin4(XLT_PADRIGHT_CMP_0_pin5), .pin5(XLT_PADRIGHT_CMP_1_pin5), .pin6(XLT_PADRIGHT_CMP_1_pin6),
    .pin7(XLT_PADRIGHT_CMP_1_pin7), .pin8(1'b0), .pin9(x_scan_b4), .pin10(PADPLUS40_ADD_1_pin4),
    .pin11(x_scan_b5), .pin12(PADPLUS40_ADD_1_pin1), .pin13(PADPLUS40_ADD_1_pin13), .pin14(x_scan_b6),
    .pin15(PADPLUS40_ADD_1_pin10), .pin16(1'b1));
  _7485 YGT460_CMP_1 (
    .pin1(1'b1), .pin2(YGT460_CMP_0_pin7), .pin3(YGT460_CMP_0_pin6), .pin4(YGT460_CMP_0_pin5),
    .pin5(YGT460_CMP_1_pin5), .pin6(YGT460_CMP_1_pin6), .pin7(YGT460_CMP_1_pin7), .pin8(1'b0), .pin9(1'b0),
    .pin10(y_scan_b4), .pin11(1'b0), .pin12(y_scan_b5), .pin13(y_scan_b6), .pin14(1'b1), .pin15(y_scan_b7),
    .pin16(1'b1));
  _7485 YLT475_CMP_1 (
    .pin1(1'b1), .pin2(YLT475_CMP_0_pin7), .pin3(YLT475_CMP_0_pin6), .pin4(YLT475_CMP_0_pin5),
    .pin5(YLT475_CMP_1_pin5), .pin6(YLT475_CMP_1_pin6), .pin7(YLT475_CMP_1_pin7), .pin8(1'b0), .pin9(1'b1),
    .pin10(y_scan_b4), .pin11(1'b0), .pin12(y_scan_b5), .pin13(y_scan_b6), .pin14(1'b1), .pin15(y_scan_b7),
    .pin16(1'b1));
  _7485 XGT_PAD_CMP_2 (
    .pin1(1'b0), .pin2(XGT_PAD_CMP_1_pin7), .pin3(XGT_PAD_CMP_1_pin6), .pin4(XGT_PAD_CMP_1_pin5),
    .pin5(XGT_PAD_CMP_2_pin5), .pin8(1'b0), .pin9(x_paddle_times_40_adder_clean_pin10), .pin10(x_scan_b8),
    .pin11(x_paddle_times_40_adder_clean_pin9), .pin12(x_scan_b9), .pin13(1'b0), .pin14(1'b0), .pin15(1'b0),
    .pin16(1'b1));  // open: pin6, pin7
  _74283 PADPLUS40_ADD_2 (
    .pin1(PADPLUS40_ADD_2_pin1), .pin2(1'b0), .pin3(x_paddle_times_40_adder_clean_pin9),
    .pin4(PADPLUS40_ADD_2_pin4), .pin5(x_paddle_times_40_adder_clean_pin10), .pin6(1'b0),
    .pin7(PADPLUS40_ADD_1_pin9), .pin8(1'b0), .pin10(PADPLUS40_ADD_2_pin10), .pin11(1'b0), .pin12(1'b0),
    .pin13(PADPLUS40_ADD_2_pin13), .pin14(1'b0), .pin15(1'b0), .pin16(1'b1));  // open: pin9
  _7485 XLT_PADRIGHT_CMP_2 (
    .pin1(1'b0), .pin2(XLT_PADRIGHT_CMP_1_pin7), .pin3(XLT_PADRIGHT_CMP_1_pin6),
    .pin4(XLT_PADRIGHT_CMP_1_pin5), .pin5(XLT_PADRIGHT_CMP_2_pin5), .pin8(1'b0), .pin9(x_scan_b8),
    .pin10(PADPLUS40_ADD_2_pin4), .pin11(x_scan_b9), .pin12(PADPLUS40_ADD_2_pin1),
    .pin13(PADPLUS40_ADD_2_pin13), .pin14(1'b0), .pin15(PADPLUS40_ADD_2_pin10), .pin16(1'b1));  // open: pin6, pin7
  _7485 YGT460_CMP_2 (
    .pin1(1'b0), .pin2(YGT460_CMP_1_pin7), .pin3(YGT460_CMP_1_pin6), .pin4(YGT460_CMP_1_pin5),
    .pin5(YGT460_CMP_2_pin5), .pin8(1'b0), .pin9(1'b1), .pin10(y_scan_b8), .pin11(1'b0), .pin12(y_scan_b9),
    .pin13(1'b0), .pin14(1'b0), .pin15(1'b0), .pin16(1'b1));  // open: pin6, pin7
  _7485 YLT475_CMP_2 (
    .pin1(1'b0), .pin2(YLT475_CMP_1_pin7), .pin3(YLT475_CMP_1_pin6), .pin4(YLT475_CMP_1_pin5),
    .pin7(YLT475_CMP_2_pin7), .pin8(1'b0), .pin9(1'b1), .pin10(y_scan_b8), .pin11(1'b0), .pin12(y_scan_b9),
    .pin13(1'b0), .pin14(1'b0), .pin15(1'b0), .pin16(1'b1));  // open: pin5, pin6
  // And PADDLE_X_WINDOW_AND has open pins: In_1=XGT_PAD_CMP_2_pin5, In_2=XLT_PADRIGHT_CMP_2_pin5, out=open
  // And PADDLE_Y_WINDOW_AND has open pins: In_1=YGT460_CMP_2_pin5, In_2=YLT475_CMP_2_pin7, out=open
  // And PADDLE_XY_FINAL_AND has open pins: In_1=paddle_x_visible, In_2=paddle_y_visible, out=open
  // Or FINAL_OR has open pins: In_1=1'b0, In_2=paddle_visible, out=open

  assign x_scan_lt_8 = x_scan_clear_n;
  assign y_scan_lt_8 = y_scan_clear_n;
  // also tied to GND on the sheet: {x_scan_cmp4_bits_0_3_pin9[0], x_scan_cmp4_bits_0_3_pin9[1], x_scan_cmp4_bits_0_3_pin9[3], x_scan_cmp4_bits_0_3_pin9[4], x_scan_cmp4_bits_0_3_pin9[5], x_scan_cmp4_bits_0_3_pin9[6], x_scan_cmp4_bits_0_3_pin9[7], x_scan_cmp4_bits_0_3_pin9[8], x_scan_cmp4_bits_0_3_pin9[9], x_scan_cmp4_bits_0_3_pin9[10], x_scan_cmp4_bits_0_3_pin9[11], x_scan_cmp6_bits_0_3_pin9[0], x_scan_cmp6_bits_0_3_pin9[3], x_scan_cmp6_bits_0_3_pin9[4], x_scan_cmp6_bits_0_3_pin9[5], x_scan_cmp6_bits_0_3_pin9[6], x_scan_cmp6_bits_0_3_pin9[7], x_scan_cmp6_bits_0_3_pin9[8], x_scan_cmp6_bits_0_3_pin9[9], x_scan_cmp6_bits_0_3_pin9[10], x_scan_cmp6_bits_0_3_pin9[11], x_scan_cmp8_bits_0_3_pin9[0], x_scan_cmp8_bits_0_3_pin9[1], x_scan_cmp8_bits_0_3_pin9[2], x_scan_cmp8_bits_0_3_pin9[4], x_scan_cmp8_bits_0_3_pin9[5], x_scan_cmp8_bits_0_3_pin9[6], x_scan_cmp8_bits_0_3_pin9[7], x_scan_cmp8_bits_0_3_pin9[8], x_scan_cmp8_bits_0_3_pin9[9], x_scan_cmp8_bits_0_3_pin9[10], x_scan_cmp8_bits_0_3_pin9[11], y_scan_cmp4_bits_0_3_pin9[0], y_scan_cmp4_bits_0_3_pin9[1], y_scan_cmp4_bits_0_3_pin9[3], y_scan_cmp4_bits_0_3_pin9[4], y_scan_cmp4_bits_0_3_pin9[5], y_scan_cmp4_bits_0_3_pin9[6], y_scan_cmp4_bits_0_3_pin9[7], y_scan_cmp4_bits_0_3_pin9[8], y_scan_cmp4_bits_0_3_pin9[9], y_scan_cmp4_bits_0_3_pin9[10], y_scan_cmp4_bits_0_3_pin9[11], y_scan_cmp6_bits_0_3_pin9[0], y_scan_cmp6_bits_0_3_pin9[3], y_scan_cmp6_bits_0_3_pin9[4], y_scan_cmp6_bits_0_3_pin9[5], y_scan_cmp6_bits_0_3_pin9[6], y_scan_cmp6_bits_0_3_pin9[7], y_scan_cmp6_bits_0_3_pin9[8], y_scan_cmp6_bits_0_3_pin9[9], y_scan_cmp6_bits_0_3_pin9[10], y_scan_cmp6_bits_0_3_pin9[11], y_scan_cmp8_bits_0_3_pin9[0], y_scan_cmp8_bits_0_3_pin9[1], y_scan_cmp8_bits_0_3_pin9[2], y_scan_cmp8_bits_0_3_pin9[4], y_scan_cmp8_bits_0_3_pin9[5], y_scan_cmp8_bits_0_3_pin9[6], y_scan_cmp8_bits_0_3_pin9[7], y_scan_cmp8_bits_0_3_pin9[8], y_scan_cmp8_bits_0_3_pin9[9], y_scan_cmp8_bits_0_3_pin9[10], y_scan_cmp8_bits_0_3_pin9[11], x_scan_cmp4_bits_0_3_pin2[0], x_scan_cmp4_bits_0_3_pin2[2], x_scan_cmp6_bits_0_3_pin2[0], x_scan_cmp6_bits_0_3_pin2[2], x_scan_cmp8_bits_0_3_pin2[0], x_scan_cmp8_bits_0_3_pin2[2], y_scan_cmp4_bits_0_3_pin2[0], y_scan_cmp4_bits_0_3_pin2[2], y_scan_cmp6_bits_0_3_pin2[0], y_scan_cmp6_bits_0_3_pin2[2], y_scan_cmp8_bits_0_3_pin2[0], y_scan_cmp8_bits_0_3_pin2[2]}
  // also tied to VCC on the sheet: {x_scan_cmp4_bits_0_3_pin9[2], x_scan_cmp6_bits_0_3_pin9[1], x_scan_cmp6_bits_0_3_pin9[2], x_scan_cmp8_bits_0_3_pin9[3], y_scan_cmp4_bits_0_3_pin9[2], y_scan_cmp6_bits_0_3_pin9[1], y_scan_cmp6_bits_0_3_pin9[2], y_scan_cmp8_bits_0_3_pin9[3], x_scan_cmp4_bits_0_3_pin2[1], x_scan_cmp6_bits_0_3_pin2[1], x_scan_cmp8_bits_0_3_pin2[1], y_scan_cmp4_bits_0_3_pin2[1], y_scan_cmp6_bits_0_3_pin2[1], y_scan_cmp8_bits_0_3_pin2[1]}

  // Notes on the sheet:
  //   X_Paddle
  //   TEST_START = 4
  //   10 bit: 0000000100
  //   4 stored as a 12-bit constant: 0000 0000 0100
  //   TEST_END = 6
  //   10 bit: 0000000110
  //   6 stored as a 12-bit constant: 0000 0000 0110
  //   TEST_LINE_END = 8
  //   12 bit: 0000 0000 1000
  //   Y clock: fronte di salita di x_scan_lt_8 (una volta per riga di prova)
  //   TEST_FRAME_END = 8
  //   X_SCAN COUNTER (10 bit usati)
  //   Y_SCAN COUNTER (10 bit usati)
  //   X_SCAN vs TEST_START
  //   X_SCAN vs TEST_END
  //   X_SCAN vs TEST_LINE_END
  //   Y_SCAN vs TEST_START
  //   Y_SCAN vs TEST_END
  //   Y_SCAN vs TEST_FRAME_END
  //   PADDLE X × 40 — SOLO WIRES
  //   X_SCAN > X_PADDLE×40
  //   X_PADDLE×40 + 40
  //   X_SCAN < X_PADDLE×40+40
  //   Y_SCAN > 460
  //   Y_SCAN < 475
endmodule
