// Digital circuit paddle_controla_74193.dig as structural Verilog
module paddle_controla_74193 (
  input  in_5,
  input  in_6,
  input  in_7,
  input  in_8,
  input  in_9,
  input  in_10,
  input  in_11,
  input  in_14,
  input  clk,
  input  in_16,
  input  in_17,
  input  in_18,
  input  in_19,
  input  in_20,
  input  in_21,
  input  in_22,
  input  in_23,
  input  in_24,
  input  in_26,
  output out_1,
  output out_2,
  output out_3,
  output out_4,
  output out_12,
  output out_13,
  output out_25
);

  wire x_scan_0_3_pin11, x_scan_0_3_pin12, x_scan_0_3_pin13, x_scan_0_3_pin14, x_scan_0_3_pin15,
       x_scan_0_4_pin11, x_scan_0_4_pin12, x_scan_0_4_pin13, x_scan_0_4_pin14, x_scan_0_4_pin15,
       x_scan_0_5_pin11, x_scan_0_5_pin12, x_scan_0_5_pin13, x_scan_0_5_pin14;

  _74193 _74193_1 (
    .pin1(in_7), .pin2(out_3), .pin3(out_4), .pin4(in_5), .pin5(in_6), .pin6(out_2), .pin7(out_1),
    .pin8(1'b0), .pin9(in_10), .pin10(in_9), .pin11(in_11), .pin12(out_12), .pin13(out_13), .pin14(in_14),
    .pin15(in_8), .pin16(1'b1));
  _74163 x_scan_0_3 (
    .pin1(in_16), .pin2(clk), .pin3(1'b0), .pin4(1'b0), .pin5(1'b0), .pin6(1'b0), .pin7(in_17), .pin8(1'b0),
    .pin9(in_18), .pin10(in_19), .pin11(x_scan_0_3_pin11), .pin12(x_scan_0_3_pin12),
    .pin13(x_scan_0_3_pin13), .pin14(x_scan_0_3_pin14), .pin15(x_scan_0_3_pin15), .pin16(1'b1));
  LED b3 (.in(x_scan_0_3_pin11));
  LED b2 (.in(x_scan_0_3_pin12));
  LED b0 (.in(x_scan_0_3_pin14));
  LED b1 (.in(x_scan_0_3_pin13));
  _74163 x_scan_0_4 (
    .pin1(in_20), .pin2(clk), .pin3(1'b0), .pin4(1'b0), .pin5(1'b0), .pin6(1'b0), .pin7(in_21), .pin8(1'b0),
    .pin9(in_22), .pin10(x_scan_0_3_pin15), .pin11(x_scan_0_4_pin11), .pin12(x_scan_0_4_pin12),
    .pin13(x_scan_0_4_pin13), .pin14(x_scan_0_4_pin14), .pin15(x_scan_0_4_pin15), .pin16(1'b1));
  LED b7 (.in(x_scan_0_4_pin11));
  LED b6 (.in(x_scan_0_4_pin12));
  LED b4 (.in(x_scan_0_4_pin14));
  LED b5 (.in(x_scan_0_4_pin13));
  _74163 x_scan_0_5 (
    .pin1(in_23), .pin2(clk), .pin3(1'b0), .pin4(1'b0), .pin5(1'b0), .pin6(1'b0), .pin7(in_24), .pin8(1'b0),
    .pin9(in_26), .pin10(x_scan_0_4_pin15), .pin11(x_scan_0_5_pin11), .pin12(x_scan_0_5_pin12),
    .pin13(x_scan_0_5_pin13), .pin14(x_scan_0_5_pin14), .pin15(out_25), .pin16(1'b1));
  LED b11 (.in(x_scan_0_5_pin11));
  LED b8 (.in(x_scan_0_5_pin14));
  LED b10 (.in(x_scan_0_5_pin12));
  LED b9 (.in(x_scan_0_5_pin13));

  // Notes on the sheet:
  //   X_Paddle
  //   X_scan
endmodule
