// Digital circuit paddle_controla_74193_named.dig as structural Verilog
module paddle_controla_74193_named (
  input  paddle_down,
  input  paddle_up,
  input  paddle_load_n,
  input  paddle_clear,
  input  paddle_q2_in,
  input  paddle_q3_in,
  input  paddle_q1_in,
  input  paddle_q0_in,
  input  pixel_clock,
  input  xscan_low_clear_n,
  input  xscan_low_enp,
  input  xscan_low_load_n,
  input  xscan_low_ent,
  input  xscan_mid_clear_n,
  input  xscan_mid_enp,
  input  xscan_mid_load_n,
  input  xscan_high_clear_n,
  input  xscan_high_enp,
  input  xscan_high_load_n,
  output paddle_d0,
  output paddle_d1,
  output paddle_d2,
  output paddle_d3,
  output paddle_borrow_out,
  output paddle_carry_out,
  output xscan_high_rco
);

  wire x_scan_bits_0_3_pin11, x_scan_bits_0_3_pin12, x_scan_bits_0_3_pin13, x_scan_bits_0_3_pin14,
       x_scan_bits_0_3_pin15, x_scan_bits_4_7_pin11, x_scan_bits_4_7_pin12, x_scan_bits_4_7_pin13,
       x_scan_bits_4_7_pin14, x_scan_bits_4_7_pin15, x_scan_bits_8_11_pin11, x_scan_bits_8_11_pin12,
       x_scan_bits_8_11_pin13, x_scan_bits_8_11_pin14;

  _74193 x_paddle_counter (
    .pin1(paddle_load_n), .pin2(paddle_d2), .pin3(paddle_d3), .pin4(paddle_down), .pin5(paddle_up),
    .pin6(paddle_d1), .pin7(paddle_d0), .pin8(1'b0), .pin9(paddle_q3_in), .pin10(paddle_q2_in),
    .pin11(paddle_q1_in), .pin12(paddle_borrow_out), .pin13(paddle_carry_out), .pin14(paddle_q0_in),
    .pin15(paddle_clear), .pin16(1'b1));
  _74163 x_scan_bits_0_3 (
    .pin1(xscan_low_clear_n), .pin2(pixel_clock), .pin3(1'b0), .pin4(1'b0), .pin5(1'b0), .pin6(1'b0),
    .pin7(xscan_low_enp), .pin8(1'b0), .pin9(xscan_low_load_n), .pin10(xscan_low_ent),
    .pin11(x_scan_bits_0_3_pin11), .pin12(x_scan_bits_0_3_pin12), .pin13(x_scan_bits_0_3_pin13),
    .pin14(x_scan_bits_0_3_pin14), .pin15(x_scan_bits_0_3_pin15), .pin16(1'b1));
  LED b3 (.in(x_scan_bits_0_3_pin11));
  LED b2 (.in(x_scan_bits_0_3_pin12));
  LED b0 (.in(x_scan_bits_0_3_pin14));
  LED b1 (.in(x_scan_bits_0_3_pin13));
  _74163 x_scan_bits_4_7 (
    .pin1(xscan_mid_clear_n), .pin2(pixel_clock), .pin3(1'b0), .pin4(1'b0), .pin5(1'b0), .pin6(1'b0),
    .pin7(xscan_mid_enp), .pin8(1'b0), .pin9(xscan_mid_load_n), .pin10(x_scan_bits_0_3_pin15),
    .pin11(x_scan_bits_4_7_pin11), .pin12(x_scan_bits_4_7_pin12), .pin13(x_scan_bits_4_7_pin13),
    .pin14(x_scan_bits_4_7_pin14), .pin15(x_scan_bits_4_7_pin15), .pin16(1'b1));
  LED b7 (.in(x_scan_bits_4_7_pin11));
  LED b6 (.in(x_scan_bits_4_7_pin12));
  LED b4 (.in(x_scan_bits_4_7_pin14));
  LED b5 (.in(x_scan_bits_4_7_pin13));
  _74163 x_scan_bits_8_11 (
    .pin1(xscan_high_clear_n), .pin2(pixel_clock), .pin3(1'b0), .pin4(1'b0), .pin5(1'b0), .pin6(1'b0),
    .pin7(xscan_high_enp), .pin8(1'b0), .pin9(xscan_high_load_n), .pin10(x_scan_bits_4_7_pin15),
    .pin11(x_scan_bits_8_11_pin11), .pin12(x_scan_bits_8_11_pin12), .pin13(x_scan_bits_8_11_pin13),
    .pin14(x_scan_bits_8_11_pin14), .pin15(xscan_high_rco), .pin16(1'b1));
  LED b11 (.in(x_scan_bits_8_11_pin11));
  LED b8 (.in(x_scan_bits_8_11_pin14));
  LED b10 (.in(x_scan_bits_8_11_pin12));
  LED b9 (.in(x_scan_bits_8_11_pin13));

  // Notes on the sheet:
  //   X_Paddle
  //   X_scan
endmodule
